// Logisim project mult32.circ as structural Verilog: 8 circuits, main circuit Multiplier_(main)
module Multiplier__main (
  input  [31:0] Multiplier,
  input  [31:0] Multiplicand,
  output [31:0] _63_32,
  output [31:0] _31_0
);

  wire alu_1_end, alu_1_pr0_1, clock_1_out, fsm_1_s1, fsm_1_s2, fsm_1_s3, fsm_1_s4, fsm_1_s5, fsm_1_s6,
       fsm_signals_1_add, fsm_signals_1_counter, fsm_signals_1_load_shifted, fsm_signals_1_shifted, go_out,
       reset_out, synchroniser_1_bo, synchroniser_2_bo;

  Button go (.out(go_out));
  Button reset (.out(reset_out));
  Synchroniser synchroniser_1 (.bi(go_out), .clock(clock_1_out), .bo(synchroniser_1_bo));
  Synchroniser synchroniser_2 (.bi(reset_out), .clock(clock_1_out), .bo(synchroniser_2_bo));
  ALU alu_1 (
    .Multiplier(Multiplier), .Multiplicand(Multiplicand), ._63_32(_63_32), ._0_31(_31_0),
    .Load_shifted(fsm_signals_1_load_shifted), .add(fsm_signals_1_add), .shifted(fsm_signals_1_shifted),
    .clock(clock_1_out), .reset(synchroniser_2_bo), .counter(fsm_signals_1_counter), .pr0_1(alu_1_pr0_1),
    .\end (alu_1_end));
  Clock clock_1 (.out(clock_1_out));
  FSM fsm_1 (
    .reset(synchroniser_2_bo), .product0(alu_1_pr0_1), .go(synchroniser_1_bo), .\end (alu_1_end),
    .clock(clock_1_out), .S1(fsm_1_s1), .S2(fsm_1_s2), .S3(fsm_1_s3), .S4(fsm_1_s4), .S5(fsm_1_s5),
    .S6(fsm_1_s6));
  FSM_Signals fsm_signals_1 (
    .S1(fsm_1_s1), .S2(fsm_1_s2), .S3(fsm_1_s3), .S4(fsm_1_s4), .S5(fsm_1_s5), .S6(fsm_1_s6),
    .shifted(fsm_signals_1_shifted), .add(fsm_signals_1_add), .load_shifted(fsm_signals_1_load_shifted),
    .counter(fsm_signals_1_counter));

  // Notes on the sheet:
  //   HOW TO PLAY
  //   _____________________
  //   Enter your inputs
  //   Push the "go" button for calculation
  //   Push the "reset" button for new calculation
endmodule

module ALU (
  input  [31:0] Multiplier,
  input  [31:0] Multiplicand,
  input  Load_shifted,
  input  add,
  input  shifted,
  input  clock,
  input  reset,
  input  counter,
  output [31:0] _63_32,
  output [31:0] _0_31,
  output pr0_1,
  output \end 
);

  wire comparator_2_eq;
  wire [31:0] multiplexer_1_out, multiplexer_2_out, multiplexer_3_out, multiplexer_4_out, multiplexer_5_out,
       n1_bit_shifter_1_shifter_output, n1_bit_shifter_2_shifter_output, n32_bit_adder_1_adder_output,
       n32_bit_adder_2_adder_output, register_1_q;

  _32_Bit_Adder u_32_bit_adder_1 (
    .adder_input_1(register_1_q), .adder_input_2(_63_32), .adder_output(n32_bit_adder_1_adder_output));
  Multiplexer #(.width(32), .enable("false")) multiplexer_1 (
    .in0(Multiplier), .in1(multiplexer_5_out), .out(multiplexer_1_out), .sel(Load_shifted));
  Multiplexer #(.width(32), .enable("false")) multiplexer_2 (
    .in0(_63_32), .in1(n32_bit_adder_1_adder_output), .out(multiplexer_2_out), .sel(add));
  Multiplexer #(.width(32), .enable("false")) multiplexer_3 (
    .in0(multiplexer_1_out), .in1(_0_31), .out(multiplexer_3_out), .sel(shifted));
  Multiplexer #(.width(32), .enable("false")) multiplexer_4 (
    .in0(multiplexer_2_out), .in1(n1_bit_shifter_2_shifter_output), .out(multiplexer_4_out),
    .sel(Load_shifted));
  Multiplexer #(.width(32), .enable("false")) multiplexer_5 (
    .in0(n1_bit_shifter_1_shifter_output), .in1(n32_bit_adder_2_adder_output), .out(multiplexer_5_out),
    .sel(comparator_2_eq));
  Register #(.width(32)) _31_0 (.D(multiplexer_3_out), .Q(_0_31), .clk(clock), .clr(reset));  // open: en
  Register #(.width(32)) register_1 (.D(Multiplicand), .Q(register_1_q), .clk(clock), .clr(reset));  // open: en
  Register #(.width(32)) _63_32_product (.D(multiplexer_4_out), .Q(_63_32), .clk(clock), .clr(reset));  // open: en
  _1_Bit_Shifter u_1_bit_shifter_1 (.shifter_input(_0_31), .shifter_output(n1_bit_shifter_1_shifter_output));
  Comparator #(.width(1), .mode("unsigned")) comparator_1 (.a(_0_31[0]), .b(1'b1), .eq(pr0_1));  // open: gt, lt
  _32_Bit_Adder u_32_bit_adder_2 (
    .adder_input_1(n1_bit_shifter_1_shifter_output), .adder_input_2(32'h80000000),
    .adder_output(n32_bit_adder_2_adder_output));
  Comparator #(.width(1)) comparator_2 (.a(1'b1), .b(_63_32[0]), .eq(comparator_2_eq));  // open: gt, lt
  _1_Bit_Shifter u_1_bit_shifter_2 (.shifter_input(_63_32), .shifter_output(n1_bit_shifter_2_shifter_output));
  Counter #(.width(6), .max('h20)) counter_1 (
    .count(counter), .carry(\end ), .clk(clock), .clr(reset));  // open: load, D, Q
endmodule

module FSM (
  input  reset,
  input  product0,
  input  go,
  input  \end ,
  input  clock,
  output S1,
  output S2,
  output S3,
  output S4,
  output S5,
  output S6
);

  wire and_1_out, and_2_out, and_3_out, and_4_out, and_5_out, and_6_out, and_7_out, and_8_out, and_9_out,
       and_10_out, and_11_out, not_1_out, not_2_out, not_3_out, not_4_out, not_5_out, not_6_out, not_7_out,
       not_8_out, not_9_out, not_10_out, not_11_out, not_12_out, not_13_out, not_14_out, not_15_out,
       not_16_out, not_17_out, not_18_out, not_19_out, not_20_out, not_21_out, not_22_out, not_23_out,
       not_24_out, not_25_out, not_26_out, not_27_out, not_28_out, S0_out;
  wire [2:0] N0_out, register_1_q;

  not not_1 (not_1_out, \end );
  not not_2 (not_2_out, go);
  not not_3 (not_3_out, product0);
  not not_4 (not_4_out, go);
  Register #(.width(3)) register_1 (.D(N0_out), .Q(register_1_q), .clk(clock));  // open: en, clr
  not not_5 (not_5_out, register_1_q[1]);
  not not_6 (not_6_out, register_1_q[0]);
  not not_7 (not_7_out, not_6_out);
  not not_8 (not_8_out, not_5_out);
  not not_9 (not_9_out, register_1_q[2]);
  not not_10 (not_10_out, not_9_out);
  not not_11 (not_11_out, reset);
  not not_12 (not_12_out, register_1_q[0]);
  and and_1 (and_1_out, not_13_out, register_1_q[1]);
  not not_13 (not_13_out, register_1_q[2]);
  not not_14 (not_14_out, register_1_q[1]);
  and and_2 (and_2_out, register_1_q[2], not_14_out, not_15_out);
  not not_15 (not_15_out, register_1_q[0]);
  and and_3 (and_3_out, \end , register_1_q[2], not_16_out, register_1_q[0]);
  not not_16 (not_16_out, register_1_q[1]);
  and and_4 (and_4_out, not_9_out, not_5_out, register_1_q[0], not_3_out, not_2_out);
  and and_5 (and_5_out, not_9_out, not_5_out, register_1_q[0], not_2_out, product0);
  and and_6 (and_6_out, register_1_q[2], not_5_out, register_1_q[0], \end );
  and and_7 (and_7_out, not_9_out, not_5_out, not_6_out, go);
  and and_8 (and_8_out, not_9_out, not_5_out, not_7_out, product0, not_4_out);
  and and_9 (and_9_out, not_10_out, not_5_out, not_6_out);
  and and_10 (and_10_out, not_10_out, not_5_out, not_7_out, not_1_out);
  and and_11 (and_11_out, not_11_out, not_12_out, register_1_q[1], register_1_q[2]);
  or N2 (N0_out[2], and_11_out, and_1_out, and_2_out, and_3_out);
  or N1 (N0_out[1], and_11_out, and_4_out, and_5_out, and_6_out);
  or N0 (N0_out[0], and_7_out, and_8_out, and_9_out, and_10_out);
  not not_17 (not_17_out, N0_out[2]);
  not not_18 (not_18_out, N0_out[1]);
  not not_19 (not_19_out, N0_out[0]);
  not not_20 (not_20_out, N0_out[2]);
  not not_21 (not_21_out, N0_out[1]);
  not not_22 (not_22_out, N0_out[2]);
  not not_23 (not_23_out, N0_out[0]);
  not not_24 (not_24_out, N0_out[2]);
  not not_25 (not_25_out, N0_out[1]);
  not not_26 (not_26_out, N0_out[0]);
  not not_27 (not_27_out, N0_out[1]);
  not not_28 (not_28_out, N0_out[0]);
  and S0 (S0_out, not_17_out, not_18_out, not_19_out);
  and u_S1 (S1, not_20_out, not_21_out, N0_out[0]);
  and u_S2 (S2, not_22_out, N0_out[1], not_23_out);
  and u_S3 (S3, not_24_out, N0_out[1], N0_out[0]);
  and u_S4 (S4, N0_out[2], not_25_out, not_26_out);
  and u_S5 (S5, N0_out[2], not_27_out, N0_out[0]);
  and u_S6 (S6, N0_out[2], N0_out[1], not_28_out);
endmodule

module FSM_Signals (
  input  S1,
  input  S2,
  input  S3,
  input  S4,
  input  S5,
  input  S6,
  output shifted,
  output add,
  output load_shifted,
  output counter
);

  or or_1 (shifted, S1, S2, S3, S5, S6);

  assign add = S3;
  assign counter = S4;
  assign load_shifted = S4;
endmodule

module Synchroniser (
  input  bi,
  input  clock,
  output bo
);

  wire and_2_out, and_3_out, not_1_out, not_2_out, not_3_out, not_4_out, not_5_out;
  wire [1:0] and_4_out, register_1_q;

  not not_1 (not_1_out, register_1_q[1]);
  and and_1 (bo, not_1_out, register_1_q[0]);
  not not_2 (not_2_out, register_1_q[1]);
  not not_3 (not_3_out, register_1_q[0]);
  not not_4 (not_4_out, register_1_q[1]);
  not not_5 (not_5_out, register_1_q[0]);
  Register #(.width(2)) register_1 (.D(and_4_out), .Q(register_1_q), .clk(clock));  // open: en, clr
  and and_2 (and_2_out, bi, not_2_out, register_1_q[0]);
  and and_3 (and_3_out, bi, not_3_out, register_1_q[1]);
  and and_4 (and_4_out[0], bi, not_4_out, not_5_out);
  or or_1 (and_4_out[1], and_2_out, and_3_out);
endmodule

module _1_Bit_Shifter (
  input  [31:0] shifter_input,
  output [31:0] shifter_output
);

  Multiplexer #(.enable("false")) multiplexer_1 (
    .in0(1'b0), .in1(shifter_input[31]), .out(shifter_output[31]), .sel(1'b0));
  Multiplexer #(.enable("false")) multiplexer_2 (
    .in0(shifter_input[31]), .in1(shifter_input[30]), .out(shifter_output[30]), .sel(1'b0));
  Multiplexer #(.enable("false")) multiplexer_3 (
    .in0(shifter_input[30]), .in1(shifter_input[29]), .out(shifter_output[29]), .sel(1'b0));
  Multiplexer #(.enable("false")) multiplexer_4 (
    .in0(shifter_input[29]), .in1(shifter_input[28]), .out(shifter_output[28]), .sel(1'b0));
  Multiplexer #(.enable("false")) multiplexer_5 (
    .in0(shifter_input[27]), .in1(shifter_input[26]), .out(shifter_output[26]), .sel(1'b0));
  Multiplexer #(.enable("false")) multiplexer_6 (
    .in0(shifter_input[28]), .in1(shifter_input[27]), .out(shifter_output[27]), .sel(1'b0));
  Multiplexer #(.enable("false")) multiplexer_7 (
    .in0(shifter_input[26]), .in1(shifter_input[25]), .out(shifter_output[25]), .sel(1'b0));
  Multiplexer #(.enable("false")) multiplexer_8 (
    .in0(shifter_input[25]), .in1(shifter_input[24]), .out(shifter_output[24]), .sel(1'b0));
  Multiplexer #(.enable("false")) multiplexer_9 (
    .in0(shifter_input[24]), .in1(shifter_input[23]), .out(shifter_output[23]), .sel(1'b0));
  Multiplexer #(.enable("false")) multiplexer_10 (
    .in0(shifter_input[23]), .in1(shifter_input[22]), .out(shifter_output[22]), .sel(1'b0));
  Multiplexer #(.enable("false")) multiplexer_11 (
    .in0(shifter_input[22]), .in1(shifter_input[21]), .out(shifter_output[21]), .sel(1'b0));
  Multiplexer #(.enable("false")) multiplexer_12 (
    .in0(shifter_input[21]), .in1(shifter_input[20]), .out(shifter_output[20]), .sel(1'b0));
  Multiplexer #(.enable("false")) multiplexer_13 (
    .in0(shifter_input[20]), .in1(shifter_input[19]), .out(shifter_output[19]), .sel(1'b0));
  Multiplexer #(.enable("false")) multiplexer_14 (
    .in0(shifter_input[19]), .in1(shifter_input[18]), .out(shifter_output[18]), .sel(1'b0));
  Multiplexer #(.enable("false")) multiplexer_15 (
    .in0(shifter_input[18]), .in1(shifter_input[17]), .out(shifter_output[17]), .sel(1'b0));
  Multiplexer #(.enable("false")) multiplexer_16 (
    .in0(shifter_input[17]), .in1(shifter_input[16]), .out(shifter_output[16]), .sel(1'b0));
  Multiplexer #(.enable("false")) multiplexer_17 (
    .in0(shifter_input[16]), .in1(shifter_input[15]), .out(shifter_output[15]), .sel(1'b0));
  Multiplexer #(.enable("false")) multiplexer_18 (
    .in0(shifter_input[15]), .in1(shifter_input[14]), .out(shifter_output[14]), .sel(1'b0));
  Multiplexer #(.enable("false")) multiplexer_19 (
    .in0(shifter_input[13]), .in1(shifter_input[12]), .out(shifter_output[12]), .sel(1'b0));
  Multiplexer #(.enable("false")) multiplexer_20 (
    .in0(shifter_input[14]), .in1(shifter_input[13]), .out(shifter_output[13]), .sel(1'b0));
  Multiplexer #(.enable("false")) multiplexer_21 (
    .in0(shifter_input[12]), .in1(shifter_input[11]), .out(shifter_output[11]), .sel(1'b0));
  Multiplexer #(.enable("false")) multiplexer_22 (
    .in0(shifter_input[11]), .in1(shifter_input[10]), .out(shifter_output[10]), .sel(1'b0));
  Multiplexer #(.enable("false")) multiplexer_23 (
    .in0(shifter_input[10]), .in1(shifter_input[9]), .out(shifter_output[9]), .sel(1'b0));
  Multiplexer #(.enable("false")) multiplexer_24 (
    .in0(shifter_input[9]), .in1(shifter_input[8]), .out(shifter_output[8]), .sel(1'b0));
  Multiplexer #(.enable("false")) multiplexer_25 (
    .in0(shifter_input[8]), .in1(shifter_input[7]), .out(shifter_output[7]), .sel(1'b0));
  Multiplexer #(.enable("false")) multiplexer_26 (
    .in0(shifter_input[6]), .in1(shifter_input[5]), .out(shifter_output[5]), .sel(1'b0));
  Multiplexer #(.enable("false")) multiplexer_27 (
    .in0(shifter_input[7]), .in1(shifter_input[6]), .out(shifter_output[6]), .sel(1'b0));
  Multiplexer #(.enable("false")) multiplexer_28 (
    .in0(shifter_input[5]), .in1(shifter_input[4]), .out(shifter_output[4]), .sel(1'b0));
  Multiplexer #(.enable("false")) multiplexer_29 (
    .in0(shifter_input[4]), .in1(shifter_input[3]), .out(shifter_output[3]), .sel(1'b0));
  Multiplexer #(.enable("false")) multiplexer_30 (
    .in0(shifter_input[3]), .in1(shifter_input[2]), .out(shifter_output[2]), .sel(1'b0));
  Multiplexer #(.enable("false")) multiplexer_31 (
    .in0(shifter_input[2]), .in1(shifter_input[1]), .out(shifter_output[1]), .sel(1'b0));
  Multiplexer #(.enable("false")) multiplexer_32 (
    .in0(shifter_input[1]), .in1(shifter_input[0]), .out(shifter_output[0]), .sel(1'b0));
endmodule

module _32_Bit_Adder (
  input  [31:0] adder_input_1,
  input  [31:0] adder_input_2,
  output [31:0] adder_output
);

  wire n1_bit_adder_1_c_o, n1_bit_adder_2_c_o, n1_bit_adder_3_c_o, n1_bit_adder_4_c_o, n1_bit_adder_5_c_o,
       n1_bit_adder_6_c_o, n1_bit_adder_7_c_o, n1_bit_adder_8_c_o, n1_bit_adder_9_c_o, n1_bit_adder_10_c_o,
       n1_bit_adder_11_c_o, n1_bit_adder_12_c_o, n1_bit_adder_13_c_o, n1_bit_adder_14_c_o,
       n1_bit_adder_15_c_o, n1_bit_adder_16_c_o, n1_bit_adder_17_c_o, n1_bit_adder_18_c_o,
       n1_bit_adder_19_c_o, n1_bit_adder_20_c_o, n1_bit_adder_21_c_o, n1_bit_adder_22_c_o,
       n1_bit_adder_23_c_o, n1_bit_adder_24_c_o, n1_bit_adder_25_c_o, n1_bit_adder_26_c_o,
       n1_bit_adder_27_c_o, n1_bit_adder_28_c_o, n1_bit_adder_29_c_o, n1_bit_adder_30_c_o,
       n1_bit_adder_31_c_o, n1_bit_adder_32_c_o;

  _1_Bit_Adder u_1_bit_adder_1 (
    .a(adder_input_1[26]), .c_i(n1_bit_adder_14_c_o), .b(adder_input_2[26]), .c_o(n1_bit_adder_1_c_o),
    .s(adder_output[26]));
  _1_Bit_Adder u_1_bit_adder_2 (
    .a(adder_input_1[27]), .c_i(n1_bit_adder_1_c_o), .b(adder_input_2[27]), .c_o(n1_bit_adder_2_c_o),
    .s(adder_output[27]));
  _1_Bit_Adder u_1_bit_adder_3 (
    .a(adder_input_1[28]), .c_i(n1_bit_adder_2_c_o), .b(adder_input_2[28]), .c_o(n1_bit_adder_3_c_o),
    .s(adder_output[28]));
  _1_Bit_Adder u_1_bit_adder_4 (
    .a(adder_input_1[29]), .c_i(n1_bit_adder_3_c_o), .b(adder_input_2[29]), .c_o(n1_bit_adder_4_c_o),
    .s(adder_output[29]));
  _1_Bit_Adder u_1_bit_adder_5 (
    .a(adder_input_1[30]), .c_i(n1_bit_adder_4_c_o), .b(adder_input_2[30]), .c_o(n1_bit_adder_5_c_o),
    .s(adder_output[30]));
  _1_Bit_Adder u_1_bit_adder_6 (
    .a(adder_input_1[31]), .c_i(n1_bit_adder_5_c_o), .b(adder_input_2[31]), .c_o(n1_bit_adder_6_c_o),
    .s(adder_output[31]));
  _1_Bit_Adder u_1_bit_adder_7 (
    .a(adder_input_1[18]), .c_i(n1_bit_adder_24_c_o), .b(adder_input_2[18]), .c_o(n1_bit_adder_7_c_o),
    .s(adder_output[18]));
  _1_Bit_Adder u_1_bit_adder_8 (
    .a(adder_input_1[19]), .c_i(n1_bit_adder_7_c_o), .b(adder_input_2[19]), .c_o(n1_bit_adder_8_c_o),
    .s(adder_output[19]));
  _1_Bit_Adder u_1_bit_adder_9 (
    .a(adder_input_1[20]), .c_i(n1_bit_adder_8_c_o), .b(adder_input_2[20]), .c_o(n1_bit_adder_9_c_o),
    .s(adder_output[20]));
  _1_Bit_Adder u_1_bit_adder_10 (
    .a(adder_input_1[21]), .c_i(n1_bit_adder_9_c_o), .b(adder_input_2[21]), .c_o(n1_bit_adder_10_c_o),
    .s(adder_output[21]));
  _1_Bit_Adder u_1_bit_adder_11 (
    .a(adder_input_1[22]), .c_i(n1_bit_adder_10_c_o), .b(adder_input_2[22]), .c_o(n1_bit_adder_11_c_o),
    .s(adder_output[22]));
  _1_Bit_Adder u_1_bit_adder_12 (
    .a(adder_input_1[23]), .c_i(n1_bit_adder_11_c_o), .b(adder_input_2[23]), .c_o(n1_bit_adder_12_c_o),
    .s(adder_output[23]));
  _1_Bit_Adder u_1_bit_adder_13 (
    .a(adder_input_1[24]), .c_i(n1_bit_adder_12_c_o), .b(adder_input_2[24]), .c_o(n1_bit_adder_13_c_o),
    .s(adder_output[24]));
  _1_Bit_Adder u_1_bit_adder_14 (
    .a(adder_input_1[25]), .c_i(n1_bit_adder_13_c_o), .b(adder_input_2[25]), .c_o(n1_bit_adder_14_c_o),
    .s(adder_output[25]));
  _1_Bit_Adder u_1_bit_adder_15 (
    .a(adder_input_1[8]), .c_i(n1_bit_adder_32_c_o), .b(adder_input_2[8]), .c_o(n1_bit_adder_15_c_o),
    .s(adder_output[8]));
  _1_Bit_Adder u_1_bit_adder_16 (
    .a(adder_input_1[9]), .c_i(n1_bit_adder_15_c_o), .b(adder_input_2[9]), .c_o(n1_bit_adder_16_c_o),
    .s(adder_output[9]));
  _1_Bit_Adder u_1_bit_adder_17 (
    .a(adder_input_1[10]), .c_i(n1_bit_adder_16_c_o), .b(adder_input_2[10]), .c_o(n1_bit_adder_17_c_o),
    .s(adder_output[10]));
  _1_Bit_Adder u_1_bit_adder_18 (
    .a(adder_input_1[11]), .c_i(n1_bit_adder_17_c_o), .b(adder_input_2[11]), .c_o(n1_bit_adder_18_c_o),
    .s(adder_output[11]));
  _1_Bit_Adder u_1_bit_adder_19 (
    .a(adder_input_1[12]), .c_i(n1_bit_adder_18_c_o), .b(adder_input_2[12]), .c_o(n1_bit_adder_19_c_o),
    .s(adder_output[12]));
  _1_Bit_Adder u_1_bit_adder_20 (
    .a(adder_input_1[13]), .c_i(n1_bit_adder_19_c_o), .b(adder_input_2[13]), .c_o(n1_bit_adder_20_c_o),
    .s(adder_output[13]));
  _1_Bit_Adder u_1_bit_adder_21 (
    .a(adder_input_1[14]), .c_i(n1_bit_adder_20_c_o), .b(adder_input_2[14]), .c_o(n1_bit_adder_21_c_o),
    .s(adder_output[14]));
  _1_Bit_Adder u_1_bit_adder_22 (
    .a(adder_input_1[15]), .c_i(n1_bit_adder_21_c_o), .b(adder_input_2[15]), .c_o(n1_bit_adder_22_c_o),
    .s(adder_output[15]));
  _1_Bit_Adder u_1_bit_adder_23 (
    .a(adder_input_1[16]), .c_i(n1_bit_adder_22_c_o), .b(adder_input_2[16]), .c_o(n1_bit_adder_23_c_o),
    .s(adder_output[16]));
  _1_Bit_Adder u_1_bit_adder_24 (
    .a(adder_input_1[17]), .c_i(n1_bit_adder_23_c_o), .b(adder_input_2[17]), .c_o(n1_bit_adder_24_c_o),
    .s(adder_output[17]));
  _1_Bit_Adder u_1_bit_adder_25 (
    .a(adder_input_1[0]), .c_i(1'b0), .b(adder_input_2[0]), .c_o(n1_bit_adder_25_c_o), .s(adder_output[0]));
  _1_Bit_Adder u_1_bit_adder_26 (
    .a(adder_input_1[1]), .c_i(n1_bit_adder_25_c_o), .b(adder_input_2[1]), .c_o(n1_bit_adder_26_c_o),
    .s(adder_output[1]));
  _1_Bit_Adder u_1_bit_adder_27 (
    .a(adder_input_1[2]), .c_i(n1_bit_adder_26_c_o), .b(adder_input_2[2]), .c_o(n1_bit_adder_27_c_o),
    .s(adder_output[2]));
  _1_Bit_Adder u_1_bit_adder_28 (
    .a(adder_input_1[3]), .c_i(n1_bit_adder_27_c_o), .b(adder_input_2[3]), .c_o(n1_bit_adder_28_c_o),
    .s(adder_output[3]));
  _1_Bit_Adder u_1_bit_adder_29 (
    .a(adder_input_1[4]), .c_i(n1_bit_adder_28_c_o), .b(adder_input_2[4]), .c_o(n1_bit_adder_29_c_o),
    .s(adder_output[4]));
  _1_Bit_Adder u_1_bit_adder_30 (
    .a(adder_input_1[5]), .c_i(n1_bit_adder_29_c_o), .b(adder_input_2[5]), .c_o(n1_bit_adder_30_c_o),
    .s(adder_output[5]));
  _1_Bit_Adder u_1_bit_adder_31 (
    .a(adder_input_1[6]), .c_i(n1_bit_adder_30_c_o), .b(adder_input_2[6]), .c_o(n1_bit_adder_31_c_o),
    .s(adder_output[6]));
  _1_Bit_Adder u_1_bit_adder_32 (
    .a(adder_input_1[7]), .c_i(n1_bit_adder_31_c_o), .b(adder_input_2[7]), .c_o(n1_bit_adder_32_c_o),
    .s(adder_output[7]));

  // Notes on the sheet:
  //   OVERFLOW (NOT REQUIRED FOR THE HW.)
endmodule

module _1_Bit_Adder (
  input  a,
  input  b,
  input  c_i,
  output s,
  output c_o
);

  wire and_1_out, and_2_out, S1_out, xor_1_out, xor_2_out;

  and and_1 (and_1_out, c_i, xor_1_out);
  xor xor_1 (xor_1_out, a, b);
  and and_2 (and_2_out, a, b);
  or or_1 (c_o, and_1_out, and_2_out);
  ExactlyOne xor_2 (.out(xor_2_out), .in0(a), .in1(c_i), .in2(b));
  and S1 (S1_out, b, c_i, a);
  or u_s (s, xor_2_out, S1_out);
endmodule
