// Logisim project 1801042630_MehmetAvniCelik.circ as structural Verilog: 4 circuits, main circuit main
module main (
  input  RESET_SCORE
);

  wire and_1_out, and_2_out, and_3_out, and_4_out, and_5_out, and_6_out, and_7_out, and_8_out, and_9_out,
       and_10_out, and_11_out, and_12_out, and_13_out, and_14_out, and_15_out, and_16_out, and_17_out,
       and_18_out, and_19_out, and_20_out, and_21_out, and_22_out, and_23_out, and_24_out, and_25_out,
       and_26_out, and_27_out, and_28_out, and_29_out, and_30_out, and_31_out, and_32_out, clock_1_out,
       not_1_out, not_2_out, not_3_out, not_4_out, not_5_out, not_6_out, not_7_out, not_8_out, not_9_out,
       not_10_out, not_11_out, not_12_out, not_13_out, not_14_out, not_15_out, not_16_out, not_17_out,
       not_18_out, not_19_out, not_20_out, not_21_out, not_22_out, not_23_out, not_24_out, not_25_out,
       not_26_out, not_27_out, not_28_out, not_29_out, not_30_out, not_31_out, not_32_out, not_33_out,
       not_34_out, not_35_out, not_36_out, not_37_out, not_38_out, not_39_out, not_40_out, not_41_out,
       not_42_out, not_43_out, not_44_out, not_45_out, not_46_out, p_out, r_out, score_1_a, score_1_b,
       score_1_c, score_1_d, score_1_e, score_1_f, score_1_g, score_2_a, score_2_b, score_2_c, score_2_d,
       score_2_e, score_2_f, score_2_g, senkronizer_1_bo, senkronizer_2_bo, senkronizer_3_bo, v_out;
  wire [2:0] or_3_out, register_1_q;
  wire [3:0] transfer_1_out, transfer_2_out;

  Button p (.out(p_out));
  senkronizer senkronizer_1 (.bi(p_out), .bo(senkronizer_1_bo));
  Button v (.out(v_out));
  senkronizer senkronizer_2 (.bi(v_out), .bo(senkronizer_2_bo));
  senkronizer senkronizer_3 (.bi(r_out), .bo(senkronizer_3_bo));
  Button r (.out(r_out));
  not not_1 (not_1_out, senkronizer_2_bo);
  not not_2 (not_2_out, senkronizer_3_bo);
  not not_3 (not_3_out, senkronizer_2_bo);
  not not_4 (not_4_out, senkronizer_3_bo);
  not not_5 (not_5_out, senkronizer_3_bo);
  not not_6 (not_6_out, senkronizer_3_bo);
  not not_7 (not_7_out, register_1_q[0]);
  not not_8 (not_8_out, senkronizer_1_bo);
  not not_9 (not_9_out, senkronizer_1_bo);
  not not_10 (not_10_out, register_1_q[1]);
  not not_11 (not_11_out, senkronizer_2_bo);
  not not_12 (not_12_out, register_1_q[0]);
  not not_13 (not_13_out, senkronizer_2_bo);
  not not_14 (not_14_out, senkronizer_1_bo);
  not not_15 (not_15_out, register_1_q[0]);
  not not_16 (not_16_out, senkronizer_1_bo);
  not not_17 (not_17_out, register_1_q[1]);
  not not_18 (not_18_out, senkronizer_1_bo);
  not not_19 (not_19_out, senkronizer_1_bo);
  not not_20 (not_20_out, senkronizer_2_bo);
  not not_21 (not_21_out, senkronizer_1_bo);
  not not_22 (not_22_out, senkronizer_2_bo);
  not not_23 (not_23_out, register_1_q[2]);
  not not_24 (not_24_out, register_1_q[0]);
  not not_25 (not_25_out, senkronizer_1_bo);
  not not_26 (not_26_out, register_1_q[2]);
  not not_27 (not_27_out, register_1_q[0]);
  not not_28 (not_28_out, senkronizer_2_bo);
  not not_29 (not_29_out, senkronizer_2_bo);
  not not_30 (not_30_out, register_1_q[1]);
  not not_31 (not_31_out, register_1_q[0]);
  not not_32 (not_32_out, senkronizer_1_bo);
  not not_33 (not_33_out, register_1_q[1]);
  not not_34 (not_34_out, register_1_q[0]);
  not not_35 (not_35_out, senkronizer_2_bo);
  and and_1 (and_1_out, register_1_q[1], register_1_q[0], senkronizer_1_bo, not_1_out, not_2_out);
  and and_2 (and_2_out, register_1_q[2], not_3_out, not_4_out);
  and and_3 (and_3_out, register_1_q[2], senkronizer_1_bo, not_5_out);
  and and_4 (and_4_out, register_1_q[2], register_1_q[0], not_6_out);
  and and_5 (and_5_out, register_1_q[2], register_1_q[1], not_7_out, not_8_out, senkronizer_2_bo);
  and and_6 (and_6_out, not_9_out, senkronizer_3_bo);
  and and_7 (and_7_out, senkronizer_2_bo, senkronizer_3_bo);
  and and_8 (and_8_out, register_1_q[0], senkronizer_3_bo);
  and and_9 (and_9_out, not_10_out, register_1_q[0], senkronizer_1_bo, not_11_out);
  and and_10 (and_10_out, register_1_q[1], not_12_out, not_13_out);
  and and_11 (and_11_out, register_1_q[1], senkronizer_1_bo, senkronizer_2_bo);
  and and_12 (and_12_out, register_1_q[1], register_1_q[0], not_14_out);
  and and_13 (and_13_out, register_1_q[2], senkronizer_3_bo);
  and and_14 (and_14_out, register_1_q[2], not_15_out, not_16_out, senkronizer_2_bo);
  and and_15 (and_15_out, not_17_out, not_18_out, senkronizer_3_bo);
  and and_16 (and_16_out, not_19_out, not_20_out, senkronizer_3_bo);
  and and_17 (and_17_out, senkronizer_1_bo, senkronizer_2_bo, senkronizer_3_bo);
  and and_18 (and_18_out, register_1_q[0], not_21_out, not_22_out);
  and and_19 (and_19_out, register_1_q[0], senkronizer_3_bo);
  and and_20 (and_20_out, register_1_q[0], senkronizer_1_bo, senkronizer_2_bo);
  and and_21 (and_21_out, not_23_out, register_1_q[1], not_24_out, not_25_out, senkronizer_2_bo);
  and and_22 (and_22_out, not_26_out, register_1_q[1], not_27_out, senkronizer_1_bo, not_28_out);
  and and_23 (and_23_out, register_1_q[2], not_29_out, senkronizer_3_bo);
  and and_24 (and_24_out, register_1_q[2], not_30_out, not_31_out, not_32_out, senkronizer_2_bo);
  and and_25 (and_25_out, register_1_q[2], not_33_out, not_34_out, senkronizer_1_bo, not_35_out);
  or or_1 (or_3_out[2], and_1_out, and_2_out, and_3_out, and_4_out, and_5_out);
  or or_2 (or_3_out[1], and_6_out, and_7_out, and_8_out, and_9_out, and_10_out, and_11_out, and_12_out, and_13_out, and_14_out);
  or or_3 (or_3_out[0], and_15_out, and_16_out, and_17_out, and_18_out, and_19_out, and_20_out, and_21_out, and_22_out, and_23_out, and_24_out, and_25_out);
  Register #(.width(3)) register_1 (.D(or_3_out), .Q(register_1_q), .clk(clock_1_out));  // open: en, clr
  Clock clock_1 (.out(clock_1_out));
  _7_Segment_Display u_7_segment_display_1 (
    .g(score_1_g), .f(score_1_f), .a(score_1_a), .b(score_1_b), .e(score_1_e), .d(score_1_d), .c(score_1_c));  // open: dp
  score score_1 (
    .s2(transfer_1_out), .a(score_1_a), .b(score_1_b), .c(score_1_c), .d(score_1_d), .e(score_1_e),
    .f(score_1_f), .g(score_1_g));
  not not_36 (not_36_out, or_3_out[2]);
  not not_37 (not_37_out, or_3_out[1]);
  not not_38 (not_38_out, or_3_out[0]);
  not not_39 (not_39_out, or_3_out[2]);
  not not_40 (not_40_out, or_3_out[1]);
  not not_41 (not_41_out, or_3_out[2]);
  not not_42 (not_42_out, or_3_out[0]);
  not not_43 (not_43_out, or_3_out[2]);
  LED led_1 (.in(and_26_out));
  transfer transfer_1 (.score(and_26_out), .out(transfer_1_out), .rr(RESET_SCORE));
  and and_26 (and_26_out, not_36_out, not_37_out, not_38_out);
  and and_27 (and_27_out, not_39_out, not_40_out, or_3_out[0]);
  and and_28 (and_28_out, not_41_out, or_3_out[1], not_42_out);
  and and_29 (and_29_out, not_43_out, or_3_out[1], or_3_out[0]);
  and and_30 (and_30_out, or_3_out[2], not_44_out, not_45_out);
  not not_44 (not_44_out, or_3_out[1]);
  not not_45 (not_45_out, or_3_out[0]);
  and and_31 (and_31_out, or_3_out[2], not_46_out, or_3_out[0]);
  not not_46 (not_46_out, or_3_out[1]);
  and and_32 (and_32_out, or_3_out[2], or_3_out[1]);
  // NOT_Gate not_47 has open pins: in=or_3_out[0], out=open
  LED led_2 (.in(and_27_out));
  LED led_3 (.in(and_26_out));
  LED led_4 (.in(and_29_out));
  LED led_5 (.in(and_28_out));
  LED led_6 (.in(and_30_out));
  LED led_7 (.in(and_31_out));
  LED led_8 (.in(and_32_out));
  LED led_9 (.in(and_32_out));
  transfer transfer_2 (.score(and_32_out), .out(transfer_2_out), .rr(RESET_SCORE));
  score score_2 (
    .s2(transfer_2_out), .a(score_2_a), .b(score_2_b), .c(score_2_c), .d(score_2_d), .e(score_2_e),
    .f(score_2_f), .g(score_2_g));
  _7_Segment_Display u_7_segment_display_2 (
    .g(score_2_g), .f(score_2_f), .a(score_2_a), .b(score_2_b), .e(score_2_e), .d(score_2_d), .c(score_2_c));  // open: dp

  // Notes on the sheet:
  //   PLAYER 1
  //   PLAYER 2
  //   RESET
  //   MEHMET AVNİ ÇELİK
  //   1801042630
  //   BUTTON PRESSING GAME 
  //   PLEASE PRESS RESET AND RESET_SCORE BUTTONS BEFORE STARTING THE GAME.
  //   AFTER THE DISPLAY SHOWS 9,YOU MUST PRESS RESET_SCORE AGAIN,OTHERWISE SCORING WILL NOT BE CORRECT
endmodule

module senkronizer (
  input  bi,
  output bo
);

  wire and_2_out, and_3_out, clock_1_out, not_1_out, not_2_out, not_3_out, not_4_out, not_5_out;
  wire [1:0] and_4_out, register_1_q;

  not not_1 (not_1_out, register_1_q[1]);
  and and_1 (bo, not_1_out, register_1_q[0]);
  not not_2 (not_2_out, register_1_q[1]);
  not not_3 (not_3_out, register_1_q[0]);
  not not_4 (not_4_out, register_1_q[1]);
  not not_5 (not_5_out, register_1_q[0]);
  Register #(.width(2)) register_1 (.D(and_4_out), .Q(register_1_q), .clk(clock_1_out));  // open: en, clr
  and and_2 (and_2_out, bi, not_2_out, register_1_q[0]);
  and and_3 (and_3_out, bi, not_3_out, register_1_q[1]);
  and and_4 (and_4_out[0], bi, not_4_out, not_5_out);
  or or_1 (and_4_out[1], and_2_out, and_3_out);
  Clock clock_1 (.out(clock_1_out));

  // Notes on the sheet:
  //   --This is the Button Press Synchronizer from chapter 3 page 47--
  //   --Go back to the main file to play the game--
endmodule

module score (
  input  [3:0] s2,
  output a,
  output b,
  output c,
  output d,
  output e,
  output f,
  output g
);

  wire and_1_out, and_2_out, and_3_out, and_4_out, and_5_out, and_6_out, and_7_out, and_8_out, and_9_out,
       and_10_out, and_11_out, and_12_out, and_13_out, and_14_out, and_15_out, and_16_out, and_17_out,
       and_18_out, and_19_out, and_20_out, and_21_out, and_22_out, and_23_out, and_24_out, and_25_out,
       and_26_out, not_1_out, not_2_out, not_3_out, not_4_out, not_5_out, not_6_out, not_7_out, not_8_out,
       not_9_out, not_10_out, not_11_out, not_12_out, not_13_out, not_14_out, not_15_out, not_16_out,
       not_17_out, not_18_out, not_19_out, not_20_out, not_21_out, not_22_out, not_23_out, not_24_out,
       not_25_out, not_26_out, not_27_out, not_28_out, not_29_out, not_30_out, not_31_out, not_32_out,
       not_33_out, not_34_out, not_35_out, not_36_out, not_37_out, not_38_out, not_39_out, not_40_out,
       not_41_out, not_42_out, not_43_out, not_44_out, not_45_out, not_46_out, not_47_out, not_48_out,
       not_49_out, not_50_out, not_51_out, not_52_out;

  not not_1 (not_1_out, s2[3]);
  not not_2 (not_2_out, s2[2]);
  not not_3 (not_3_out, s2[0]);
  not not_4 (not_4_out, s2[3]);
  not not_5 (not_5_out, s2[3]);
  not not_6 (not_6_out, s2[2]);
  not not_7 (not_7_out, s2[1]);
  not not_8 (not_8_out, s2[3]);
  not not_9 (not_9_out, s2[2]);
  not not_10 (not_10_out, s2[3]);
  not not_11 (not_11_out, s2[1]);
  not not_12 (not_12_out, s2[0]);
  not not_13 (not_13_out, s2[2]);
  not not_14 (not_14_out, s2[1]);
  not not_15 (not_15_out, s2[3]);
  not not_16 (not_16_out, s2[2]);
  not not_17 (not_17_out, s2[1]);
  not not_18 (not_18_out, s2[3]);
  not not_19 (not_19_out, s2[3]);
  not not_20 (not_20_out, s2[3]);
  not not_21 (not_21_out, s2[2]);
  not not_22 (not_22_out, s2[0]);
  not not_23 (not_23_out, s2[3]);
  not not_24 (not_24_out, s2[2]);
  not not_25 (not_25_out, s2[3]);
  not not_26 (not_26_out, s2[0]);
  not not_27 (not_27_out, s2[3]);
  not not_28 (not_28_out, s2[1]);
  not not_29 (not_29_out, s2[2]);
  not not_30 (not_30_out, s2[1]);
  not not_31 (not_31_out, s2[2]);
  not not_32 (not_32_out, s2[1]);
  not not_33 (not_33_out, s2[0]);
  not not_34 (not_34_out, s2[3]);
  not not_35 (not_35_out, s2[0]);
  not not_36 (not_36_out, s2[3]);
  not not_37 (not_37_out, s2[1]);
  not not_38 (not_38_out, s2[0]);
  not not_39 (not_39_out, s2[3]);
  not not_40 (not_40_out, s2[1]);
  not not_41 (not_41_out, s2[3]);
  not not_42 (not_42_out, s2[0]);
  not not_43 (not_43_out, s2[2]);
  not not_44 (not_44_out, s2[1]);
  not not_45 (not_45_out, s2[3]);
  not not_46 (not_46_out, s2[2]);
  not not_47 (not_47_out, s2[3]);
  not not_48 (not_48_out, s2[1]);
  not not_49 (not_49_out, s2[3]);
  not not_50 (not_50_out, s2[0]);
  not not_51 (not_51_out, s2[2]);
  not not_52 (not_52_out, s2[1]);
  and and_1 (and_1_out, not_1_out, not_2_out, not_3_out);
  and and_2 (and_2_out, not_4_out, s2[1]);
  and and_3 (and_3_out, not_5_out, s2[2], s2[0]);
  and and_4 (and_4_out, s2[3], not_6_out, not_7_out);
  and and_5 (and_5_out, not_8_out, not_9_out);
  and and_6 (and_6_out, not_10_out, not_11_out, not_12_out);
  and and_7 (and_7_out, not_13_out, not_14_out);
  and and_8 (and_8_out, not_15_out, s2[1], s2[0]);
  and and_9 (and_9_out, not_16_out, not_17_out);
  and and_10 (and_10_out, not_18_out, s2[0]);
  and and_11 (and_11_out, not_19_out, s2[2]);
  and and_12 (and_12_out, not_20_out, not_21_out, not_22_out);
  and and_13 (and_13_out, not_23_out, not_24_out, s2[1]);
  and and_14 (and_14_out, not_25_out, s2[1], not_26_out);
  and and_15 (and_15_out, not_27_out, s2[2], not_28_out, s2[0]);
  and and_16 (and_16_out, s2[3], not_29_out, not_30_out);
  and and_17 (and_17_out, not_31_out, not_32_out, not_33_out);
  and and_18 (and_18_out, not_34_out, s2[1], not_35_out);
  and and_19 (and_19_out, not_36_out, not_37_out, not_38_out);
  and and_20 (and_20_out, not_39_out, s2[2], not_40_out);
  and and_21 (and_21_out, not_41_out, s2[2], not_42_out);
  and and_22 (and_22_out, s2[3], not_43_out, not_44_out);
  and and_23 (and_23_out, not_45_out, not_46_out, s2[1]);
  and and_24 (and_24_out, not_47_out, s2[2], not_48_out);
  and and_25 (and_25_out, not_49_out, s2[2], not_50_out);
  and and_26 (and_26_out, s2[3], not_51_out, not_52_out);
  or or_1 (a, and_1_out, and_2_out, and_3_out, and_4_out);
  or or_2 (b, and_5_out, and_6_out, and_7_out, and_8_out);
  or or_3 (c, and_9_out, and_10_out, and_11_out);
  or or_4 (d, and_12_out, and_13_out, and_14_out, and_15_out, and_16_out);
  or or_5 (e, and_17_out, and_18_out);
  or or_6 (f, and_19_out, and_20_out, and_21_out, and_22_out);
  or or_7 (g, and_23_out, and_24_out, and_25_out, and_26_out);
endmodule

module transfer (
  input  score,
  input  rr,
  output [3:0] out
);

  wire senkronizer_1_bo, senkronizer_2_bo;
  wire [3:0] bit_extender_1_out;

  senkronizer senkronizer_1 (.bi(score), .bo(senkronizer_1_bo));
  senkronizer senkronizer_2 (.bi(score), .bo(senkronizer_2_bo));
  assign bit_extender_1_out = {{3{1'b0}}, senkronizer_1_bo};  // Bit_Extender bit_extender_1
  Counter #(.width(4), .max('hf)) counter_1 (
    .D(bit_extender_1_out), .Q(out), .clk(senkronizer_2_bo), .clr(rr));  // open: load, count, carry
endmodule
