// Logisim project 1801042630_2.circ as structural Verilog: 8 circuits, main circuit main
module main (
  input  a,
  input  b,
  input  c,
  input  d,
  input  e,
  input  f,
  input  g,
  input  h,
  input  i,
  input  j,
  input  k,
  input  l,
  input  m,
  input  n,
  input  o,
  input  p,
  input  q,
  input  r,
  input  s,
  input  t,
  input  u,
  input  w,
  input  v,
  input  x,
  input  y,
  input  z,
  input  [7:0] L0,
  input  [7:0] L1,
  input  [7:0] L2,
  input  [7:0] L3,
  input  [7:0] L4,
  input  [7:0] L5,
  input  [7:0] L6,
  input  [7:0] L7,
  input  on_off,
  input  DELETE_SCORES,
  input  RESET_PREVIOUS,
  output WIN,
  output LOSE
);

  wire and_1_out, clock_1_out, control_unit_1_go, control_unit_1_reset, control_unit_1_show,
       control_unit_1_wrong, datapath_1__8t, datapath_1_done, datapath_1_length, datapath_1_p_2,
       datapath_1_w1, datapath_1_w2, datapath_1_w3, datapath_1_w4, datapath_1_w5, datapath_1_w6,
       datapath_1_w7, datapath_1_w8, datapath_1_w9, datapath_1_w10, datapath_1_w_out, scoredisplay_1_a,
       scoredisplay_1_b, scoredisplay_1_c, scoredisplay_1_d, scoredisplay_1_e, scoredisplay_1_f,
       scoredisplay_1_g, scoredisplay_2_a, scoredisplay_2_b, scoredisplay_2_c, scoredisplay_2_d,
       scoredisplay_2_e, scoredisplay_2_f, scoredisplay_2_g, scoredisplay_3_a, scoredisplay_3_b,
       scoredisplay_3_c, scoredisplay_3_d, scoredisplay_3_e, scoredisplay_3_f, scoredisplay_3_g,
       synchroniser_1_bo;
  wire [6:0] display_1_print, display_2_print, multiplexer_9_out;
  wire [7:0] datapath_1_c0, datapath_1_c1, datapath_1_c2, datapath_1_c3, datapath_1_c4, datapath_1_c5,
       datapath_1_c6, datapath_1_c7, datapath_1_c8, multiplexer_1_out, multiplexer_2_out, multiplexer_3_out,
       multiplexer_4_out, multiplexer_5_out, multiplexer_6_out, multiplexer_7_out, multiplexer_8_out,
       register_2_q, register_3_q, register_4_q, register_5_q, register_6_q, register_7_q, register_8_q,
       register_9_q;
  wire [9:0] hangman_1_h1, hangman_1_h2, hangman_1_h3, hangman_1_h4, hangman_1_h5, hangman_1_h6,
       hangman_1_h7, hangman_1_h8, hangman_1_h9, hangman_1_h10;

  Multiplexer #(.width(8), .enable("false")) multiplexer_1 (
    .in0(L0), .in1({8{1'b0}}), .out(multiplexer_1_out), .sel(RESET_PREVIOUS));
  Multiplexer #(.width(8), .enable("false")) multiplexer_2 (
    .in0(L1), .in1({8{1'b0}}), .out(multiplexer_2_out), .sel(RESET_PREVIOUS));
  Multiplexer #(.width(8), .enable("false")) multiplexer_3 (
    .in0(L2), .in1({8{1'b0}}), .out(multiplexer_3_out), .sel(RESET_PREVIOUS));
  Multiplexer #(.width(8), .enable("false")) multiplexer_4 (
    .in0(L3), .in1({8{1'b0}}), .out(multiplexer_4_out), .sel(RESET_PREVIOUS));
  Multiplexer #(.width(8), .enable("false")) multiplexer_5 (
    .in0(L4), .in1({8{1'b0}}), .out(multiplexer_5_out), .sel(RESET_PREVIOUS));
  Multiplexer #(.width(8), .enable("false")) multiplexer_6 (
    .in0(L5), .in1({8{1'b0}}), .out(multiplexer_6_out), .sel(RESET_PREVIOUS));
  Multiplexer #(.width(8), .enable("false")) multiplexer_7 (
    .in0(L6), .in1({8{1'b0}}), .out(multiplexer_7_out), .sel(RESET_PREVIOUS));
  Multiplexer #(.width(8), .enable("false")) multiplexer_8 (
    .in0(L7), .in1({8{1'b0}}), .out(multiplexer_8_out), .sel(RESET_PREVIOUS));
  Display display_1 (
    .show(LOSE), .c0(multiplexer_1_out), .c1(multiplexer_2_out), .c2(multiplexer_3_out),
    .c3(multiplexer_4_out), .c4(multiplexer_5_out), .c5(multiplexer_6_out), .c6(multiplexer_7_out),
    .c7(multiplexer_8_out), .reset(RESET_PREVIOUS), .print(display_1_print), .clock(clock_1_out));  // open: c8
  Datapath datapath_1 (
    .L0(multiplexer_1_out), .L1(multiplexer_2_out), .L2(multiplexer_3_out), .L3(multiplexer_4_out),
    .L4(multiplexer_5_out), .L5(multiplexer_6_out), .L6(multiplexer_7_out), .L7(multiplexer_8_out),
    .go(control_unit_1_go), .wrong_inp(control_unit_1_wrong), .clear_wrongs(RESET_PREVIOUS), .a(a), .b(b),
    .c(c), .d(d), .e(e), .f(f), .g(g), .h(h), .i(i), .j(j), .k(k), .l(l), .m(m), .n(n), .o(o), .p(p), .q(q),
    .r(r), .s(s), .t(t), .u(u), .w(w), .v(v), .x(x), .y(y), .z(z), .p_2(datapath_1_p_2), .clock(clock_1_out),
    .show(control_unit_1_show), ._8t(datapath_1__8t), .C0(datapath_1_c0), .C1(datapath_1_c1),
    .C2(datapath_1_c2), .C3(datapath_1_c3), .C4(datapath_1_c4), .C5(datapath_1_c5), .C6(datapath_1_c6),
    .C7(datapath_1_c7), .C8(datapath_1_c8), .w_out(datapath_1_w_out), .done(datapath_1_done),
    .length(datapath_1_length), .w1(datapath_1_w1), .w2(datapath_1_w2), .w3(datapath_1_w3),
    .w4(datapath_1_w4), .w5(datapath_1_w5), .w6(datapath_1_w6), .w7(datapath_1_w7), .w8(datapath_1_w8),
    .w9(datapath_1_w9), .w10(datapath_1_w10));
  Clock clock_1 (.out(clock_1_out));
  Control_Unit control_unit_1 (
    .on(on_off), .w(datapath_1_w_out), .done(datapath_1_done), .lost(datapath_1_w10), .p(datapath_1_p_2),
    ._8t_i(datapath_1__8t), .clock(clock_1_out), .go(control_unit_1_go), .show(control_unit_1_show),
    .reset(control_unit_1_reset), .win(WIN), .wrong(control_unit_1_wrong), .lose(LOSE));
  Register register_1 (.clk(clock_1_out));  // open: D, en, Q, clr
  Register register_2 (.D(datapath_1_c1), .Q(register_2_q), .clk(clock_1_out));  // open: en, clr
  Register register_3 (.D(datapath_1_c2), .Q(register_3_q), .clk(clock_1_out));  // open: en, clr
  Register register_4 (.D(datapath_1_c3), .Q(register_4_q), .clk(clock_1_out));  // open: en, clr
  Register register_5 (.D(datapath_1_c4), .Q(register_5_q), .clk(clock_1_out));  // open: en, clr
  Register register_6 (.D(datapath_1_c5), .Q(register_6_q), .clk(clock_1_out));  // open: en, clr
  Register register_7 (.D(datapath_1_c6), .Q(register_7_q), .clk(clock_1_out));  // open: en, clr
  Register register_8 (.D(datapath_1_c7), .Q(register_8_q), .clk(clock_1_out));  // open: en, clr
  Register register_9 (.D(datapath_1_c8), .Q(register_9_q), .clk(clock_1_out));  // open: en, clr
  Display display_2 (
    .show(control_unit_1_show), .c0(datapath_1_c0), .c1(register_2_q), .c2(register_3_q), .c3(register_4_q),
    .c4(register_5_q), .c5(register_6_q), .c6(register_7_q), .c7(register_8_q), .c8(register_9_q),
    .reset(control_unit_1_reset), .print(display_2_print), .clock(clock_1_out));
  ScoreDisplay scoredisplay_1 (
    .Pulse(datapath_1_length), .Reset_Score(RESET_PREVIOUS), .a(scoredisplay_1_a), .b(scoredisplay_1_b),
    .c(scoredisplay_1_c), .d(scoredisplay_1_d), .e(scoredisplay_1_e), .f(scoredisplay_1_f),
    .g(scoredisplay_1_g));
  LED led_1 (.in(datapath_1_w4));
  LED led_2 (.in(datapath_1_w3));
  LED led_3 (.in(datapath_1_w1));
  LED led_4 (.in(datapath_1_w2));
  _7_Segment_Display u_7_segment_display_1 (
    .g(scoredisplay_1_g), .f(scoredisplay_1_f), .a(scoredisplay_1_a), .b(scoredisplay_1_b),
    .e(scoredisplay_1_e), .d(scoredisplay_1_d), .c(scoredisplay_1_c));  // open: dp
  Multiplexer #(.width(7), .enable("false")) multiplexer_9 (
    .in0(display_2_print), .in1(display_1_print), .out(multiplexer_9_out), .sel(and_1_out));
  and and_1 (and_1_out, LOSE, on_off);
  LED led_5 (.in(datapath_1_w6));
  LED led_6 (.in(datapath_1_w5));
  LED led_7 (.in(datapath_1_w8));
  LED led_8 (.in(datapath_1_w7));
  TTY tty_1 (.data(multiplexer_9_out), .clk(clock_1_out), .clr(RESET_PREVIOUS));  // open: we
  LED led_9 (.in(datapath_1_w10));
  LED led_10 (.in(datapath_1_w9));
  ScoreDisplay scoredisplay_2 (
    .Pulse(WIN), .Reset_Score(DELETE_SCORES), .a(scoredisplay_2_a), .b(scoredisplay_2_b),
    .c(scoredisplay_2_c), .d(scoredisplay_2_d), .e(scoredisplay_2_e), .f(scoredisplay_2_f),
    .g(scoredisplay_2_g));
  Synchroniser synchroniser_1 (.bi(datapath_1_w_out), .bo(synchroniser_1_bo));
  HangMan hangman_1 (
    .x(synchroniser_1_bo), .clear(RESET_PREVIOUS), .h1(hangman_1_h1), .h2(hangman_1_h2), .h3(hangman_1_h3),
    .h4(hangman_1_h4), .h5(hangman_1_h5), .h6(hangman_1_h6), .h7(hangman_1_h7), .h8(hangman_1_h8),
    .h9(hangman_1_h9), .h10(hangman_1_h10));
  _7_Segment_Display u_7_segment_display_2 (
    .g(scoredisplay_2_g), .f(scoredisplay_2_f), .a(scoredisplay_2_a), .b(scoredisplay_2_b),
    .e(scoredisplay_2_e), .d(scoredisplay_2_d), .c(scoredisplay_2_c));  // open: dp
  DotMatrix #(.matrixcols(10), .matrixrows(10)) dotmatrix_1 (
    .col0(hangman_1_h1), .col1(hangman_1_h2), .col2(hangman_1_h3), .col3(hangman_1_h4), .col4(hangman_1_h5),
    .col5(hangman_1_h6), .col6(hangman_1_h7), .col7(hangman_1_h8), .col8(hangman_1_h9), .col9(hangman_1_h10));
  ScoreDisplay scoredisplay_3 (
    .Pulse(LOSE), .Reset_Score(DELETE_SCORES), .a(scoredisplay_3_a), .b(scoredisplay_3_b),
    .c(scoredisplay_3_c), .d(scoredisplay_3_d), .e(scoredisplay_3_e), .f(scoredisplay_3_f),
    .g(scoredisplay_3_g));
  _7_Segment_Display u_7_segment_display_3 (
    .g(scoredisplay_3_g), .f(scoredisplay_3_f), .a(scoredisplay_3_a), .b(scoredisplay_3_b),
    .e(scoredisplay_3_e), .d(scoredisplay_3_d), .c(scoredisplay_3_c));  // open: dp

  // Notes on the sheet:
  //   1) ACTIVATE THE CLOCK
  //   2) TYPE THE LETTERS IN Lx
  //   3) ACTIVATE THE "ON/OFF" BUTTON
  //   4) MAKE A GUESS UNTIL YOU WIN OR LOST
  //   4) TYPE THE LETTERS IN Lx
  //   5) ACTIVATE THE "ON/OFF" BUTTON
  //   __________TO PLAY AGAIN__________
  //   1) PUSH THE "RESET_PREVIOUS" BUTTON
  //   2) REACTIVATE THE ON/OFF BUTTON,MAKE ALL INPUTS 0 
  //   3) DEACTIVATE ON/OFF BUTTON AND FREE RESET_PREVIOUS
  //   Mehmet Avni ÇELİK
  //   1801042630
  //   LENGTH
  //   PLAYER
  //   MACHINE
endmodule

module Keyboard (
  input  a,
  input  b,
  input  c,
  input  d,
  input  e,
  input  f,
  input  g,
  input  h,
  input  i,
  input  j,
  input  k,
  input  l,
  input  m,
  input  n,
  input  o,
  input  p,
  input  q,
  input  r,
  input  s,
  input  t,
  input  u,
  input  v,
  input  w,
  input  x,
  input  y,
  input  z,
  output [7:0] char
);

  wire [4:0] bit_extender_1_out;
  wire [7:0] adder_1_out, adder_2_out, adder_3_out, adder_4_out, adder_5_out, adder_6_out, adder_7_out,
       adder_8_out, adder_9_out, adder_10_out, adder_11_out, adder_12_out, adder_13_out, adder_14_out,
       adder_15_out, adder_16_out, adder_17_out, adder_18_out, adder_19_out, adder_20_out, adder_21_out,
       adder_22_out, adder_23_out, adder_24_out, adder_25_out, multiplexer_1_out, multiplexer_2_out,
       multiplexer_3_out, multiplexer_4_out, multiplexer_5_out, multiplexer_6_out, multiplexer_7_out,
       multiplexer_8_out, multiplexer_9_out, multiplexer_10_out, multiplexer_11_out, multiplexer_12_out,
       multiplexer_13_out, multiplexer_14_out, multiplexer_15_out, multiplexer_16_out, multiplexer_17_out,
       multiplexer_18_out, multiplexer_19_out, multiplexer_20_out, multiplexer_21_out, multiplexer_22_out,
       multiplexer_23_out, multiplexer_24_out, multiplexer_25_out, multiplexer_26_out;

  Multiplexer #(.width(8), .enable("false")) multiplexer_1 (
    .in0(adder_15_out), .in1({8{1'b0}}), .out(multiplexer_1_out), .sel(n));
  Multiplexer #(.width(8), .enable("false")) multiplexer_2 (
    .in0(8'h1), .in1({8{1'b0}}), .out(multiplexer_2_out), .sel(z));
  Multiplexer #(.width(8), .enable("false")) multiplexer_3 (
    .in0(adder_12_out), .in1({8{1'b0}}), .out(multiplexer_3_out), .sel(w));
  Adder adder_1 (.a(8'h1), .b(multiplexer_4_out), .out(adder_1_out));  // open: cin, cout
  Multiplexer #(.width(8), .enable("false")) multiplexer_4 (
    .in0(adder_13_out), .in1({8{1'b0}}), .out(multiplexer_4_out), .sel(t));
  Multiplexer #(.width(8), .enable("false")) multiplexer_5 (
    .in0(adder_14_out), .in1({8{1'b0}}), .out(multiplexer_5_out), .sel(q));
  Adder adder_2 (.a(8'h1), .b(multiplexer_1_out), .out(adder_2_out));  // open: cin, cout
  Adder adder_3 (.a(8'h1), .b(multiplexer_2_out), .out(adder_3_out));  // open: cin, cout
  Adder adder_4 (.a(8'h1), .b(multiplexer_3_out), .out(adder_4_out));  // open: cin, cout
  Multiplexer #(.width(8), .enable("false")) multiplexer_6 (
    .in0(adder_1_out), .in1({8{1'b0}}), .out(multiplexer_6_out), .sel(s));
  Adder adder_5 (.a(8'h1), .b(multiplexer_5_out), .out(adder_5_out));  // open: cin, cout
  Multiplexer #(.width(8), .enable("false")) multiplexer_7 (
    .in0(adder_2_out), .in1({8{1'b0}}), .out(multiplexer_7_out), .sel(m));
  Multiplexer #(.width(8), .enable("false")) multiplexer_8 (
    .in0(adder_3_out), .in1({8{1'b0}}), .out(multiplexer_8_out), .sel(y));
  Multiplexer #(.width(8), .enable("false")) multiplexer_9 (
    .in0(adder_4_out), .in1({8{1'b0}}), .out(multiplexer_9_out), .sel(v));
  Multiplexer #(.width(8), .enable("false")) multiplexer_10 (
    .in0(adder_5_out), .in1({8{1'b0}}), .out(multiplexer_10_out), .sel(p));
  Adder adder_6 (.a(8'h1), .b(multiplexer_8_out), .out(adder_6_out));  // open: cin, cout
  Adder adder_7 (.a(8'h1), .b(multiplexer_9_out), .out(adder_7_out));  // open: cin, cout
  Adder adder_8 (.a(8'h1), .b(multiplexer_6_out), .out(adder_8_out));  // open: cin, cout
  Adder adder_9 (.a(8'h1), .b(multiplexer_10_out), .out(adder_9_out));  // open: cin, cout
  Adder adder_10 (.a(8'h1), .b(multiplexer_7_out), .out(adder_10_out));  // open: cin, cout
  Multiplexer #(.width(8), .enable("false")) multiplexer_11 (
    .in0(adder_6_out), .in1({8{1'b0}}), .out(multiplexer_11_out), .sel(x));
  Multiplexer #(.width(8), .enable("false")) multiplexer_12 (
    .in0(adder_7_out), .in1({8{1'b0}}), .out(multiplexer_12_out), .sel(u));
  Multiplexer #(.width(8), .enable("false")) multiplexer_13 (
    .in0(adder_8_out), .in1({8{1'b0}}), .out(multiplexer_13_out), .sel(r));
  Multiplexer #(.width(8), .enable("false")) multiplexer_14 (
    .in0(adder_9_out), .in1({8{1'b0}}), .out(multiplexer_14_out), .sel(o));
  Adder adder_11 (.a(8'h1), .b(multiplexer_15_out), .out(adder_11_out));  // open: cin, cout
  Multiplexer #(.width(8), .enable("false")) multiplexer_15 (
    .in0(adder_10_out), .in1({8{1'b0}}), .out(multiplexer_15_out), .sel(l));
  Adder adder_12 (.a(8'h1), .b(multiplexer_11_out), .out(adder_12_out));  // open: cin, cout
  Adder adder_13 (.a(8'h1), .b(multiplexer_12_out), .out(adder_13_out));  // open: cin, cout
  Adder adder_14 (.a(8'h1), .b(multiplexer_13_out), .out(adder_14_out));  // open: cin, cout
  Adder adder_15 (.a(8'h1), .b(multiplexer_14_out), .out(adder_15_out));  // open: cin, cout
  Multiplexer #(.width(8), .enable("false")) multiplexer_16 (
    .in0(adder_11_out), .in1({8{1'b0}}), .out(multiplexer_16_out), .sel(k));
  Multiplexer #(.width(8), .enable("false")) multiplexer_17 (
    .in0(adder_23_out), .in1({8{1'b0}}), .out(multiplexer_17_out), .sel(h));
  Adder adder_16 (.a(8'h1), .b(multiplexer_18_out), .out(adder_16_out));  // open: cin, cout
  Multiplexer #(.width(8), .enable("false")) multiplexer_18 (
    .in0(adder_24_out), .in1({8{1'b0}}), .out(multiplexer_18_out), .sel(e));
  Multiplexer #(.width(8), .enable("false")) multiplexer_19 (
    .in0(adder_25_out), .in1({8{1'b0}}), .out(multiplexer_19_out), .sel(b));
  Adder adder_17 (.a(8'h1), .b(multiplexer_16_out), .out(adder_17_out));  // open: cin, cout
  Adder adder_18 (.a(8'h1), .b(multiplexer_17_out), .out(adder_18_out));  // open: cin, cout
  Multiplexer #(.width(8), .enable("false")) multiplexer_20 (
    .in0(adder_16_out), .in1({8{1'b0}}), .out(multiplexer_20_out), .sel(d));
  Adder adder_19 (.a(8'h1), .b(multiplexer_19_out), .out(adder_19_out));  // open: cin, cout
  Multiplexer #(.width(8), .enable("false")) multiplexer_21 (
    .in0(adder_17_out), .in1({8{1'b0}}), .out(multiplexer_21_out), .sel(j));
  Multiplexer #(.width(8), .enable("false")) multiplexer_22 (
    .in0(adder_18_out), .in1({8{1'b0}}), .out(multiplexer_22_out), .sel(g));
  Multiplexer #(.width(8), .enable("false")) multiplexer_23 (
    .in0(adder_19_out), .in1({8{1'b0}}), .out(multiplexer_23_out), .sel(a));
  Adder adder_20 (.a(8'h1), .b(multiplexer_21_out), .out(adder_20_out));  // open: cin, cout
  Adder adder_21 (.a(8'h1), .b(multiplexer_22_out), .out(adder_21_out));  // open: cin, cout
  Adder adder_22 (.a(8'h1), .b(multiplexer_20_out), .out(adder_22_out));  // open: cin, cout
  Bit_Extender #(.out_width(5)) bit_extender_1 (.in(multiplexer_23_out), .out(bit_extender_1_out));
  Multiplexer #(.width(8), .enable("false")) multiplexer_24 (
    .in0(adder_20_out), .in1({8{1'b0}}), .out(multiplexer_24_out), .sel(i));
  Multiplexer #(.width(8), .enable("false")) multiplexer_25 (
    .in0(adder_21_out), .in1({8{1'b0}}), .out(multiplexer_25_out), .sel(f));
  Multiplexer #(.width(8), .enable("false")) multiplexer_26 (
    .in0(adder_22_out), .in1({8{1'b0}}), .out(multiplexer_26_out), .sel(c));
  Multiplexer #(.select(5), .width(8), .enable("false")) multiplexer_27 (
    .in0(8'h61), .in1(8'h62), .in2(8'h63), .in3(8'h64), .in4(8'h65), .in5(8'h66), .in6(8'h67), .in7(8'h68),
    .in8(8'h69), .in9(8'h6a), .in10(8'h6b), .in11(8'h6c), .in12(8'h6d), .in13(8'h6e), .in14(8'h6f),
    .in15(8'h70), .in16(8'h71), .in17(8'h72), .in18(8'h73), .in19(8'h74), .in20(8'h75), .in21(8'h76),
    .in22(8'h77), .in23(8'h78), .in24(8'h79), .in25(8'h7a), .in26({8{1'b0}}), .in27({8{1'b0}}),
    .in28({8{1'b0}}), .in29({8{1'b0}}), .in30({8{1'b0}}), .in31({8{1'b0}}), .out(char),
    .sel(bit_extender_1_out));
  Adder adder_23 (.a(8'h1), .b(multiplexer_24_out), .out(adder_23_out));  // open: cin, cout
  Adder adder_24 (.a(8'h1), .b(multiplexer_25_out), .out(adder_24_out));  // open: cin, cout
  Adder adder_25 (.a(8'h1), .b(multiplexer_26_out), .out(adder_25_out));  // open: cin, cout
endmodule

module Datapath (
  input  [7:0] L0,
  input  [7:0] L1,
  input  [7:0] L2,
  input  [7:0] L3,
  input  [7:0] L4,
  input  [7:0] L5,
  input  [7:0] L6,
  input  [7:0] L7,
  input  a,
  input  b,
  input  c,
  input  d,
  input  e,
  input  f,
  input  g,
  input  h,
  input  i,
  input  j,
  input  k,
  input  l,
  input  m,
  input  n,
  input  o,
  input  p,
  input  q,
  input  r,
  input  s,
  input  t,
  input  u,
  input  w,
  input  v,
  input  x,
  input  y,
  input  z,
  input  clock,
  input  go,
  input  wrong_inp,
  input  clear_wrongs,
  input  show,
  output [7:0] C0,
  output [7:0] C1,
  output [7:0] C2,
  output [7:0] C3,
  output [7:0] C4,
  output [7:0] C5,
  output [7:0] C6,
  output [7:0] C7,
  output [7:0] C8,
  output w_out,
  output done,
  output p_2,
  output length,
  output w1,
  output w2,
  output w3,
  output w4,
  output w5,
  output w6,
  output w7,
  output w8,
  output w9,
  output _8t,
  output w10
);

  wire comparator_1_lt, comparator_2_lt, comparator_3_lt, comparator_4_lt, comparator_5_lt, comparator_6_lt,
       comparator_7_lt, comparator_8_lt, comparator_9_lt, comparator_10_lt, comparator_11_eq,
       comparator_12_eq, comparator_13_eq, comparator_14_eq, comparator_15_eq, comparator_16_eq,
       comparator_17_eq, comparator_18_eq, comparator_19_eq, comparator_20_lt, comparator_21_eq,
       comparator_22_eq, comparator_23_eq, comparator_24_eq, comparator_25_eq, comparator_26_eq,
       comparator_27_eq, comparator_28_eq, multiplexer_1_out, N1_out, not_11_out, not_12_out, not_13_out,
       not_14_out, not_15_out, not_16_out, not_17_out, not_18_out, not_19_out, or_1_out, or_2_out, or_3_out,
       or_4_out, or_5_out, or_6_out, or_7_out, or_8_out, synchroniser_2_bo, synchroniser_3_bo,
       synchroniser_4_bo, synchroniser_5_bo, synchroniser_6_bo, synchroniser_7_bo, synchroniser_8_bo,
       synchroniser_9_bo;
  wire [7:0] counter_1_q, counter_2_q, keyboard_1_char, multiplexer_2_out, multiplexer_3_out,
       multiplexer_4_out, multiplexer_5_out, multiplexer_6_out, multiplexer_7_out, multiplexer_8_out,
       multiplexer_9_out, register_1_q, register_2_q, register_3_q, register_4_q, register_5_q, register_6_q,
       register_7_q, register_8_q, register_9_q;

  or N1 (N1_out, 1'b0, a, n, m, b, l, k, c, j, i, d, h, g, e, f, o, p, q, r, s, t, u, w, v, x, y, z);
  Synchroniser synchroniser_1 (.bi(N1_out), .bo(p_2));
  Keyboard keyboard_1 (
    .a(a), .b(b), .c(c), .d(d), .e(e), .f(f), .g(g), .h(h), .i(i), .j(j), .k(k), .l(l), .m(m), .n(n), .o(o),
    .p(p), .q(q), .r(r), .s(s), .t(t), .u(u), .v(w), .w(v), .x(x), .y(y), .z(z), .char(keyboard_1_char));
  Register register_1 (.D(keyboard_1_char), .en(go), .Q(register_1_q), .clk(clock));  // open: clr
  Counter counter_1 (.Q(counter_1_q), .clk(wrong_inp), .clr(clear_wrongs));  // open: load, D, count, carry
  Comparator comparator_1 (.a(counter_1_q), .b(8'h1), .lt(comparator_1_lt));  // open: gt, eq
  Comparator comparator_2 (.a(counter_1_q), .b(8'h2), .lt(comparator_2_lt));  // open: gt, eq
  Comparator comparator_3 (.a(counter_1_q), .b(8'h3), .lt(comparator_3_lt));  // open: gt, eq
  Comparator comparator_4 (.a(counter_1_q), .b(8'h4), .lt(comparator_4_lt));  // open: gt, eq
  Comparator comparator_5 (.a(counter_1_q), .b(8'h5), .lt(comparator_5_lt));  // open: gt, eq
  Comparator comparator_6 (.a(counter_1_q), .b(8'h6), .lt(comparator_6_lt));  // open: gt, eq
  Comparator comparator_7 (.a(counter_1_q), .b(8'h7), .lt(comparator_7_lt));  // open: gt, eq
  Comparator comparator_8 (.a(counter_1_q), .b(8'h8), .lt(comparator_8_lt));  // open: gt, eq
  Comparator comparator_9 (.a(counter_1_q), .b(8'h9), .lt(comparator_9_lt));  // open: gt, eq
  Comparator comparator_10 (.a(counter_1_q), .b(8'ha), .lt(comparator_10_lt));  // open: gt, eq
  not not_1 (w1, comparator_1_lt);
  not not_2 (w2, comparator_2_lt);
  not not_3 (w3, comparator_3_lt);
  not not_4 (w4, comparator_4_lt);
  not not_5 (w5, comparator_5_lt);
  not not_6 (w6, comparator_6_lt);
  not not_7 (w7, comparator_7_lt);
  not not_8 (w8, comparator_8_lt);
  not not_9 (w9, comparator_9_lt);
  not not_10 (w10, comparator_10_lt);
  Comparator comparator_11 (.a(L0), .b(register_1_q), .eq(comparator_11_eq));  // open: gt, lt
  Comparator comparator_12 (.a(L1), .b(register_1_q), .eq(comparator_12_eq));  // open: gt, lt
  Comparator comparator_13 (.a(L2), .b(register_1_q), .eq(comparator_13_eq));  // open: gt, lt
  Comparator comparator_14 (.a(L3), .b(register_1_q), .eq(comparator_14_eq));  // open: gt, lt
  Comparator comparator_15 (.a(L4), .b(register_1_q), .eq(comparator_15_eq));  // open: gt, lt
  Comparator comparator_16 (.a(L5), .b(register_1_q), .eq(comparator_16_eq));  // open: gt, lt
  Comparator comparator_17 (.a(L6), .b(register_1_q), .eq(comparator_17_eq));  // open: gt, lt
  Comparator comparator_18 (.a(L7), .b(register_1_q), .eq(comparator_18_eq));  // open: gt, lt
  Comparator comparator_19 (.a(register_1_q), .b({8{1'b0}}), .eq(comparator_19_eq));  // open: gt, lt
  not not_11 (not_11_out, comparator_11_eq);
  not not_12 (not_12_out, comparator_12_eq);
  not not_13 (not_13_out, comparator_13_eq);
  not not_14 (not_14_out, comparator_14_eq);
  not not_15 (not_15_out, comparator_15_eq);
  not not_16 (not_16_out, comparator_16_eq);
  not not_17 (not_17_out, comparator_17_eq);
  not not_18 (not_18_out, comparator_18_eq);
  not not_19 (not_19_out, comparator_19_eq);
  Multiplexer #(.enable("false")) multiplexer_1 (.in0(1'b0), .in1(clock), .out(multiplexer_1_out), .sel(show));
  and and_1 (w_out, not_11_out, not_12_out, not_13_out, not_14_out, not_19_out, not_15_out, not_16_out, not_17_out, not_18_out);
  Counter counter_2 (.Q(counter_2_q), .clk(multiplexer_1_out), .clr(comparator_20_lt));  // open: load, D, count, carry
  Multiplexer #(.width(8), .enable("false")) multiplexer_2 (
    .in0(register_2_q), .in1(L0), .out(multiplexer_2_out), .sel(comparator_11_eq));
  Multiplexer #(.width(8), .enable("false")) multiplexer_3 (
    .in0(register_3_q), .in1(L1), .out(multiplexer_3_out), .sel(comparator_12_eq));
  Multiplexer #(.width(8), .enable("false")) multiplexer_4 (
    .in0(register_4_q), .in1(L2), .out(multiplexer_4_out), .sel(comparator_13_eq));
  Multiplexer #(.width(8), .enable("false")) multiplexer_5 (
    .in0(register_5_q), .in1(L3), .out(multiplexer_5_out), .sel(comparator_14_eq));
  Multiplexer #(.width(8), .enable("false")) multiplexer_6 (
    .in0(register_6_q), .in1(L4), .out(multiplexer_6_out), .sel(comparator_15_eq));
  Multiplexer #(.width(8), .enable("false")) multiplexer_7 (
    .in0(register_7_q), .in1(L5), .out(multiplexer_7_out), .sel(comparator_16_eq));
  Multiplexer #(.width(8), .enable("false")) multiplexer_8 (
    .in0(register_8_q), .in1(L6), .out(multiplexer_8_out), .sel(comparator_17_eq));
  Multiplexer #(.width(8), .enable("false")) multiplexer_9 (
    .in0(register_9_q), .in1(L7), .out(multiplexer_9_out), .sel(comparator_18_eq));
  Comparator comparator_20 (.a(8'h9), .b(counter_2_q), .eq(_8t), .lt(comparator_20_lt));  // open: gt
  Register register_2 (.D(multiplexer_2_out), .Q(register_2_q), .clk(clock));  // open: en, clr
  Register register_3 (.D(multiplexer_3_out), .Q(register_3_q), .clk(clock));  // open: en, clr
  Register register_4 (.D(multiplexer_4_out), .Q(register_4_q), .clk(clock));  // open: en, clr
  Register register_5 (.D(multiplexer_5_out), .Q(register_5_q), .clk(clock));  // open: en, clr
  Register register_6 (.D(multiplexer_6_out), .Q(register_6_q), .clk(clock));  // open: en, clr
  Register register_7 (.D(multiplexer_7_out), .Q(register_7_q), .clk(clock));  // open: en, clr
  Register register_8 (.D(multiplexer_8_out), .Q(register_8_q), .clk(clock));  // open: en, clr
  Register register_9 (.D(multiplexer_9_out), .Q(register_9_q), .clk(clock));  // open: en, clr
  Comparator comparator_21 (.a(L0), .b(register_2_q), .eq(comparator_21_eq));  // open: gt, lt
  Comparator comparator_22 (.a(L1), .b(register_3_q), .eq(comparator_22_eq));  // open: gt, lt
  Comparator comparator_23 (.a(L2), .b(register_4_q), .eq(comparator_23_eq));  // open: gt, lt
  Comparator comparator_24 (.a(L3), .b(register_5_q), .eq(comparator_24_eq));  // open: gt, lt
  Comparator comparator_25 (.a(L4), .b(register_6_q), .eq(comparator_25_eq));  // open: gt, lt
  Comparator comparator_26 (.a(L5), .b(register_7_q), .eq(comparator_26_eq));  // open: gt, lt
  Comparator comparator_27 (.a(L6), .b(register_8_q), .eq(comparator_27_eq));  // open: gt, lt
  Comparator comparator_28 (.a(L7), .b(register_9_q), .eq(comparator_28_eq));  // open: gt, lt
  Multiplexer #(.width(8), .enable("false")) multiplexer_10 (
    .in0(8'h5f), .in1(register_2_q), .out(C0), .sel(comparator_21_eq));
  Multiplexer #(.width(8), .enable("false")) multiplexer_11 (
    .in0(8'h5f), .in1(register_3_q), .out(C1), .sel(comparator_22_eq));
  Multiplexer #(.width(8), .enable("false")) multiplexer_12 (
    .in0(8'h5f), .in1(register_4_q), .out(C2), .sel(comparator_23_eq));
  Multiplexer #(.width(8), .enable("false")) multiplexer_13 (
    .in0(8'h5f), .in1(register_5_q), .out(C3), .sel(comparator_24_eq));
  Multiplexer #(.width(8), .enable("false")) multiplexer_14 (
    .in0(8'h5f), .in1(register_6_q), .out(C4), .sel(comparator_25_eq));
  Multiplexer #(.width(8), .enable("false")) multiplexer_15 (
    .in0(8'h5f), .in1(register_7_q), .out(C5), .sel(comparator_26_eq));
  Multiplexer #(.width(8), .enable("false")) multiplexer_16 (
    .in0(8'h5f), .in1(register_8_q), .out(C6), .sel(comparator_27_eq));
  Multiplexer #(.width(8), .enable("false")) multiplexer_17 (
    .in0(8'h5f), .in1(register_9_q), .out(C7), .sel(comparator_28_eq));
  and and_2 (done, comparator_21_eq, comparator_22_eq, comparator_23_eq, comparator_24_eq, comparator_25_eq, comparator_26_eq, comparator_27_eq, comparator_28_eq);
  Synchroniser synchroniser_2 (.bi(or_1_out), .bo(synchroniser_2_bo));
  or or_1 (or_1_out, L0[0], L0[1], L0[2], L0[3], L0[4], L0[5], L0[6], L0[7]);
  Synchroniser synchroniser_3 (.bi(or_2_out), .bo(synchroniser_3_bo));
  or or_2 (or_2_out, L1[0], L1[1], L1[2], L1[3], L1[4], L1[5], L1[6], L1[7]);
  Synchroniser synchroniser_4 (.bi(or_3_out), .bo(synchroniser_4_bo));
  or or_3 (or_3_out, L2[0], L2[1], L2[2], L2[3], L2[4], L2[5], L2[6], L2[7]);
  Synchroniser synchroniser_5 (.bi(or_4_out), .bo(synchroniser_5_bo));
  or or_4 (or_4_out, L3[0], L3[1], L3[2], L3[3], L3[4], L3[5], L3[6], L3[7]);
  Synchroniser synchroniser_6 (.bi(or_5_out), .bo(synchroniser_6_bo));
  or or_5 (or_5_out, L4[0], L4[1], L4[2], L4[3], L4[4], L4[5], L4[6], L4[7]);
  or or_6 (or_6_out, L5[0], L5[1], L5[2], L5[3], L5[4], L5[5], L5[6], L5[7]);
  Synchroniser synchroniser_7 (.bi(or_6_out), .bo(synchroniser_7_bo));
  Synchroniser synchroniser_8 (.bi(or_7_out), .bo(synchroniser_8_bo));
  or or_7 (or_7_out, L6[0], L6[1], L6[2], L6[3], L6[4], L6[5], L6[6], L6[7]);
  or or_8 (or_8_out, L7[0], L7[1], L7[2], L7[3], L7[4], L7[5], L7[6], L7[7]);
  Synchroniser synchroniser_9 (.bi(or_8_out), .bo(synchroniser_9_bo));
  or or_9 (length, synchroniser_2_bo, synchroniser_3_bo, synchroniser_4_bo, synchroniser_5_bo, synchroniser_6_bo, synchroniser_7_bo, synchroniser_8_bo, synchroniser_9_bo);

  assign C8 = 8'ha;
endmodule

module Control_Unit (
  input  on,
  input  w,
  input  done,
  input  lost,
  input  p,
  input  _8t_i,
  input  clock,
  output go,
  output show,
  output reset,
  output win,
  output wrong,
  output lose
);

  wire and_1_out, and_2_out, and_3_out, and_4_out, and_5_out, and_6_out, and_7_out, and_8_out, and_9_out,
       and_10_out, and_11_out, and_12_out, and_13_out, and_14_out, and_15_out, N0_out, N1_out, N2_out,
       not_1_out, not_2_out, not_3_out, not_4_out, not_5_out, not_6_out, not_7_out, not_8_out, not_9_out,
       not_10_out, not_11_out, not_12_out, not_13_out, not_14_out, not_15_out, not_16_out, not_17_out,
       not_18_out, not_19_out, not_20_out, not_21_out, not_22_out, not_23_out, not_24_out, not_25_out,
       not_26_out, not_27_out, not_28_out, not_29_out, not_30_out, not_31_out, not_32_out, not_33_out,
       not_34_out, not_35_out, not_36_out, not_37_out, not_38_out;
  wire [2:0] and_17_out, register_1_q;

  Register #(.width(3)) register_1 (.D(and_17_out), .Q(register_1_q), .clk(clock));  // open: en, clr
  not not_1 (not_1_out, _8t_i);
  not not_2 (not_2_out, register_1_q[2]);
  not not_3 (not_3_out, register_1_q[0]);
  and and_1 (and_1_out, register_1_q[2], not_4_out, not_5_out);
  not not_4 (not_4_out, register_1_q[1]);
  not not_5 (not_5_out, register_1_q[0]);
  and and_2 (and_2_out, register_1_q[2], register_1_q[1], not_6_out);
  not not_6 (not_6_out, register_1_q[0]);
  and and_3 (and_3_out, not_1_out, not_2_out, register_1_q[1], not_3_out);
  not not_7 (not_7_out, register_1_q[2]);
  not not_8 (not_8_out, register_1_q[1]);
  not not_9 (not_9_out, register_1_q[1]);
  not not_10 (not_10_out, register_1_q[2]);
  not not_11 (not_11_out, register_1_q[1]);
  not not_12 (not_12_out, w);
  not not_13 (not_13_out, register_1_q[2]);
  not not_14 (not_14_out, register_1_q[0]);
  not not_15 (not_15_out, register_1_q[1]);
  not not_16 (not_16_out, register_1_q[2]);
  not not_17 (not_17_out, register_1_q[1]);
  not not_18 (not_18_out, register_1_q[0]);
  not not_19 (not_19_out, register_1_q[2]);
  not not_20 (not_20_out, register_1_q[0]);
  not not_21 (not_21_out, register_1_q[2]);
  not not_22 (not_22_out, done);
  not not_23 (not_23_out, register_1_q[2]);
  not not_24 (not_24_out, register_1_q[1]);
  not not_25 (not_25_out, register_1_q[1]);
  not not_26 (not_26_out, lost);
  and and_4 (and_4_out, done, not_7_out, register_1_q[1], register_1_q[0]);
  and and_5 (and_5_out, not_7_out, not_8_out, p, register_1_q[0], w);
  and and_6 (and_6_out, register_1_q[2], not_9_out, register_1_q[0], lost);
  and and_7 (and_7_out, not_10_out, not_11_out, p, register_1_q[0], not_12_out);
  and and_8 (and_8_out, not_13_out, register_1_q[1], _8t_i, not_14_out);
  and and_9 (and_9_out, register_1_q[2], not_15_out, register_1_q[0], lost);
  and and_10 (and_10_out, on, not_16_out, not_17_out, not_18_out);
  and and_11 (and_11_out, not_19_out, register_1_q[1], not_20_out, _8t_i);
  and and_12 (and_12_out, not_21_out, register_1_q[1], register_1_q[0], not_22_out);
  and and_13 (and_13_out, not_23_out, not_24_out, p, register_1_q[0], w);
  and and_14 (and_14_out, register_1_q[2], not_25_out, register_1_q[0], not_26_out);
  not not_27 (not_27_out, register_1_q[2]);
  not not_28 (not_28_out, register_1_q[1]);
  and and_15 (and_15_out, not_27_out, not_28_out, register_1_q[0], not_29_out);
  not not_29 (not_29_out, p);
  or N1 (N1_out, and_7_out, and_8_out, and_3_out, and_9_out, and_2_out);
  or N2 (N2_out, and_4_out, and_5_out, and_2_out, and_6_out, and_1_out);
  and and_16 (and_17_out[1], on, N1_out);
  and and_17 (and_17_out[0], on, N0_out);
  or N0 (N0_out, and_10_out, and_11_out, and_12_out, and_13_out, and_14_out, and_15_out);
  and and_18 (and_17_out[2], on, N2_out);
  not not_30 (not_30_out, register_1_q[2]);
  not not_31 (not_31_out, register_1_q[1]);
  not not_32 (not_32_out, register_1_q[2]);
  not not_33 (not_33_out, register_1_q[0]);
  not not_34 (not_34_out, register_1_q[2]);
  not not_35 (not_35_out, register_1_q[1]);
  not not_36 (not_36_out, register_1_q[0]);
  not not_37 (not_37_out, register_1_q[1]);
  not not_38 (not_38_out, register_1_q[0]);
  and and_19 (go, not_30_out, not_31_out, register_1_q[0]);
  and and_20 (show, not_32_out, register_1_q[1], not_33_out);
  and and_21 (reset, not_34_out, register_1_q[1], register_1_q[0]);
  and and_22 (win, register_1_q[2], not_35_out, not_36_out);
  and and_23 (wrong, register_1_q[2], not_37_out, register_1_q[0]);
  and and_24 (lose, register_1_q[2], register_1_q[1], not_38_out);
endmodule

module Display (
  input  show,
  input  reset,
  input  [7:0] c0,
  input  [7:0] c1,
  input  [7:0] c2,
  input  [7:0] c3,
  input  [7:0] c4,
  input  [7:0] c5,
  input  [7:0] c6,
  input  [7:0] c7,
  input  [7:0] c8,
  input  clock,
  output [6:0] print
);

  wire and_1_out, comparator_1_eq, comparator_2_eq, not_1_out, not_2_out;
  wire [3:0] counter_1_q;
  wire [6:0] bit_extender_1_out, bit_extender_2_out, bit_extender_3_out, bit_extender_4_out,
       bit_extender_5_out, bit_extender_6_out, bit_extender_7_out, bit_extender_8_out, multiplexer_1_out;

  Comparator #(.width(4)) comparator_1 (.a(4'b1010), .b(counter_1_q), .eq(comparator_1_eq));  // open: gt, lt
  not not_1 (not_1_out, comparator_1_eq);
  and and_1 (and_1_out, not_1_out, show, clock);
  Bit_Extender #(.out_width(7)) bit_extender_1 (.in(c0), .out(bit_extender_1_out));
  Bit_Extender #(.out_width(7)) bit_extender_2 (.in(c1), .out(bit_extender_2_out));
  Bit_Extender #(.out_width(7)) bit_extender_3 (.in(c2), .out(bit_extender_3_out));
  Bit_Extender #(.out_width(7)) bit_extender_4 (.in(c3), .out(bit_extender_4_out));
  Bit_Extender #(.out_width(7)) bit_extender_5 (.in(c4), .out(bit_extender_5_out));
  Bit_Extender #(.out_width(7)) bit_extender_6 (.in(c5), .out(bit_extender_6_out));
  Bit_Extender #(.out_width(7)) bit_extender_7 (.in(c6), .out(bit_extender_7_out));
  Bit_Extender #(.out_width(7)) bit_extender_8 (.in(c7), .out(bit_extender_8_out));
  Bit_Extender #(.out_width(7)) bit_extender_9 (.in(c8));  // open: out
  Counter #(.width(4), .max('hf)) counter_1 (
    .Q(counter_1_q), .clk(and_1_out), .clr(reset));  // open: load, D, count, carry
  Comparator #(.width(4)) comparator_2 (.a(4'b1010), .b(counter_1_q), .eq(comparator_2_eq));  // open: gt, lt
  Multiplexer #(.select(4), .width(7), .enable("false")) multiplexer_1 (
    .in0({7{1'b0}}), .in1(bit_extender_1_out), .in2(bit_extender_2_out), .in3(bit_extender_3_out),
    .in4(bit_extender_4_out), .in5(bit_extender_5_out), .in6(bit_extender_6_out), .in7(bit_extender_7_out),
    .in8(bit_extender_8_out), .in9(7'b0001010), .out(multiplexer_1_out), .sel(counter_1_q));  // open: in10, in11, in12, in13, in14, in15
  not not_2 (not_2_out, comparator_2_eq);
  Multiplexer #(.width(7), .enable("false")) multiplexer_2 (
    .in0({7{1'b0}}), .in1(multiplexer_1_out), .out(print), .sel(not_2_out));
endmodule

module Synchroniser (
  input  bi,
  output bo
);

  wire and_2_out, and_3_out, clock_1_out, not_1_out, not_2_out, not_3_out, not_4_out, not_5_out;
  wire [1:0] and_4_out, register_1_q;

  not not_1 (not_1_out, register_1_q[1]);
  not not_2 (not_2_out, register_1_q[1]);
  not not_3 (not_3_out, register_1_q[0]);
  not not_4 (not_4_out, register_1_q[1]);
  not not_5 (not_5_out, register_1_q[0]);
  Register #(.width(2)) register_1 (.D(and_4_out), .Q(register_1_q), .clk(clock_1_out));  // open: en, clr
  Clock clock_1 (.out(clock_1_out));
  and and_1 (bo, not_1_out, register_1_q[0]);
  and and_2 (and_2_out, bi, not_2_out, register_1_q[0]);
  and and_3 (and_3_out, bi, not_3_out, register_1_q[1]);
  and and_4 (and_4_out[0], bi, not_4_out, not_5_out);
  or or_1 (and_4_out[1], and_2_out, and_3_out);

  // Notes on the sheet:
  //   --This is the Button Press Synchronizer from chapter 3 page 47--
  //   --Go back to the main file to play the game--
endmodule

module ScoreDisplay (
  input  Pulse,
  input  Reset_Score,
  output a,
  output b,
  output c,
  output d,
  output e,
  output f,
  output g
);

  wire and_1_out, and_2_out, and_3_out, and_4_out, and_5_out, and_6_out, and_7_out, and_8_out, and_9_out,
       and_10_out, and_11_out, and_12_out, and_13_out, and_14_out, and_15_out, and_16_out, and_17_out,
       and_18_out, and_19_out, and_20_out, and_21_out, and_22_out, and_23_out, and_24_out, and_25_out,
       and_26_out, not_1_out, not_2_out, not_3_out, not_4_out, not_5_out, not_6_out, not_7_out, not_8_out,
       not_9_out, not_10_out, not_11_out, not_12_out, not_13_out, not_14_out, not_15_out, not_16_out,
       not_17_out, not_18_out, not_19_out, not_20_out, not_21_out, not_22_out, not_23_out, not_24_out,
       not_25_out, not_26_out, not_27_out, not_28_out, not_29_out, not_30_out, not_31_out, not_32_out,
       not_33_out, not_34_out, not_35_out, not_36_out, not_37_out, not_38_out, not_39_out, not_40_out,
       not_41_out, not_42_out, not_43_out, not_44_out, not_45_out, not_46_out, not_47_out, not_48_out,
       not_49_out, not_50_out, not_51_out, not_52_out, synchroniser_1_bo, synchroniser_2_bo;
  wire [3:0] bit_extender_1_out, counter_1_q;

  Synchroniser synchroniser_1 (.bi(Pulse), .bo(synchroniser_1_bo));
  Synchroniser synchroniser_2 (.bi(Pulse), .bo(synchroniser_2_bo));
  assign bit_extender_1_out = {{3{1'b0}}, synchroniser_1_bo};  // Bit_Extender bit_extender_1
  Counter #(.width(4), .max('hf)) counter_1 (
    .D(bit_extender_1_out), .Q(counter_1_q), .clk(synchroniser_2_bo), .clr(Reset_Score));  // open: load, count, carry
  not not_1 (not_1_out, counter_1_q[3]);
  not not_2 (not_2_out, counter_1_q[2]);
  and and_1 (and_1_out, not_1_out, not_2_out, not_3_out);
  not not_3 (not_3_out, counter_1_q[0]);
  not not_4 (not_4_out, counter_1_q[3]);
  and and_2 (and_2_out, not_4_out, counter_1_q[1]);
  not not_5 (not_5_out, counter_1_q[3]);
  and and_3 (and_3_out, not_5_out, counter_1_q[2], counter_1_q[0]);
  not not_6 (not_6_out, counter_1_q[2]);
  and and_4 (and_4_out, counter_1_q[3], not_6_out, not_7_out);
  not not_7 (not_7_out, counter_1_q[1]);
  not not_8 (not_8_out, counter_1_q[3]);
  and and_5 (and_5_out, not_8_out, not_9_out);
  not not_9 (not_9_out, counter_1_q[2]);
  not not_10 (not_10_out, counter_1_q[3]);
  and and_6 (and_6_out, not_10_out, not_11_out, not_12_out);
  not not_11 (not_11_out, counter_1_q[1]);
  not not_12 (not_12_out, counter_1_q[0]);
  not not_13 (not_13_out, counter_1_q[2]);
  and and_7 (and_7_out, not_13_out, not_14_out);
  not not_14 (not_14_out, counter_1_q[1]);
  not not_15 (not_15_out, counter_1_q[3]);
  and and_8 (and_8_out, not_15_out, counter_1_q[1], counter_1_q[0]);
  not not_16 (not_16_out, counter_1_q[2]);
  and and_9 (and_9_out, not_16_out, not_17_out);
  not not_17 (not_17_out, counter_1_q[1]);
  not not_18 (not_18_out, counter_1_q[3]);
  and and_10 (and_10_out, not_18_out, counter_1_q[0]);
  not not_19 (not_19_out, counter_1_q[3]);
  and and_11 (and_11_out, not_19_out, counter_1_q[2]);
  not not_20 (not_20_out, counter_1_q[3]);
  not not_21 (not_21_out, counter_1_q[2]);
  not not_22 (not_22_out, counter_1_q[0]);
  not not_23 (not_23_out, counter_1_q[3]);
  not not_24 (not_24_out, counter_1_q[2]);
  not not_25 (not_25_out, counter_1_q[3]);
  not not_26 (not_26_out, counter_1_q[0]);
  not not_27 (not_27_out, counter_1_q[3]);
  not not_28 (not_28_out, counter_1_q[1]);
  not not_29 (not_29_out, counter_1_q[2]);
  not not_30 (not_30_out, counter_1_q[1]);
  not not_31 (not_31_out, counter_1_q[2]);
  and and_12 (and_12_out, not_31_out, not_32_out, not_33_out);
  not not_32 (not_32_out, counter_1_q[1]);
  not not_33 (not_33_out, counter_1_q[0]);
  not not_34 (not_34_out, counter_1_q[3]);
  and and_13 (and_13_out, not_34_out, counter_1_q[1], not_35_out);
  not not_35 (not_35_out, counter_1_q[0]);
  not not_36 (not_36_out, counter_1_q[3]);
  not not_37 (not_37_out, counter_1_q[1]);
  and and_14 (and_14_out, not_36_out, not_37_out, not_38_out);
  not not_38 (not_38_out, counter_1_q[0]);
  not not_39 (not_39_out, counter_1_q[3]);
  and and_15 (and_15_out, not_39_out, counter_1_q[2], not_40_out);
  not not_40 (not_40_out, counter_1_q[1]);
  not not_41 (not_41_out, counter_1_q[3]);
  and and_16 (and_16_out, not_41_out, counter_1_q[2], not_42_out);
  not not_42 (not_42_out, counter_1_q[0]);
  and and_17 (and_17_out, counter_1_q[3], not_43_out, not_44_out);
  not not_43 (not_43_out, counter_1_q[2]);
  not not_44 (not_44_out, counter_1_q[1]);
  not not_45 (not_45_out, counter_1_q[3]);
  not not_46 (not_46_out, counter_1_q[2]);
  and and_18 (and_18_out, not_45_out, not_46_out, counter_1_q[1]);
  not not_47 (not_47_out, counter_1_q[3]);
  and and_19 (and_19_out, not_47_out, counter_1_q[2], not_48_out);
  not not_48 (not_48_out, counter_1_q[1]);
  not not_49 (not_49_out, counter_1_q[3]);
  and and_20 (and_20_out, not_49_out, counter_1_q[2], not_50_out);
  not not_50 (not_50_out, counter_1_q[0]);
  not not_51 (not_51_out, counter_1_q[2]);
  and and_21 (and_21_out, counter_1_q[3], not_51_out, not_52_out);
  not not_52 (not_52_out, counter_1_q[1]);
  or or_1 (a, and_1_out, and_2_out, and_3_out, and_4_out);
  or or_2 (b, and_5_out, and_6_out, and_7_out, and_8_out);
  or or_3 (c, and_9_out, and_10_out, and_11_out);
  and and_22 (and_22_out, not_20_out, not_21_out, not_22_out);
  and and_23 (and_23_out, not_23_out, not_24_out, counter_1_q[1]);
  and and_24 (and_24_out, not_25_out, counter_1_q[1], not_26_out);
  and and_25 (and_25_out, not_27_out, counter_1_q[2], not_28_out, counter_1_q[0]);
  and and_26 (and_26_out, counter_1_q[3], not_29_out, not_30_out);
  or or_4 (e, and_12_out, and_13_out);
  or or_5 (f, and_14_out, and_15_out, and_16_out, and_17_out);
  or or_6 (g, and_18_out, and_19_out, and_20_out, and_21_out);
  or or_7 (d, and_22_out, and_23_out, and_24_out, and_25_out, and_26_out);
endmodule

module HangMan (
  input  x,
  input  clear,
  output [9:0] h1,
  output [9:0] h2,
  output [9:0] h3,
  output [9:0] h4,
  output [9:0] h5,
  output [9:0] h6,
  output [9:0] h7,
  output [9:0] h8,
  output [9:0] h9,
  output [9:0] h10
);

  wire comparator_1_lt, comparator_2_lt, comparator_3_lt, comparator_4_lt, comparator_5_lt, comparator_6_lt,
       comparator_7_lt, comparator_8_lt, comparator_9_lt, comparator_10_lt, comparator_11_lt, not_1_out,
       not_2_out, not_3_out, not_4_out, not_5_out, not_6_out, not_7_out, not_8_out, not_9_out, not_10_out,
       not_11_out;
  wire [9:0] counter_1_q;

  Counter #(.width(10), .max('h3ff)) counter_1 (.Q(counter_1_q), .clk(x), .clr(clear));  // open: load, D, count, carry
  Comparator #(.width(10), .mode("unsigned")) comparator_1 (
    .a({10{1'b0}}), .b(counter_1_q), .lt(comparator_1_lt));  // open: gt, eq
  Comparator #(.width(10), .mode("unsigned")) comparator_2 (
    .a(10'h1), .b(counter_1_q), .lt(comparator_2_lt));  // open: gt, eq
  Comparator #(.width(10), .mode("unsigned")) comparator_3 (
    .a(10'h2), .b(counter_1_q), .lt(comparator_3_lt));  // open: gt, eq
  Comparator #(.width(10), .mode("unsigned")) comparator_4 (
    .a(10'h3), .b(counter_1_q), .lt(comparator_4_lt));  // open: gt, eq
  Comparator #(.width(10), .mode("unsigned")) comparator_5 (
    .a(10'h4), .b(counter_1_q), .lt(comparator_5_lt));  // open: gt, eq
  Comparator #(.width(10), .mode("unsigned")) comparator_6 (
    .a(10'h5), .b(counter_1_q), .lt(comparator_6_lt));  // open: gt, eq
  Comparator #(.width(10), .mode("unsigned")) comparator_7 (
    .a(10'h6), .b(counter_1_q), .lt(comparator_7_lt));  // open: gt, eq
  Comparator #(.width(10), .mode("unsigned")) comparator_8 (
    .a(10'h7), .b(counter_1_q), .lt(comparator_8_lt));  // open: gt, eq
  Comparator #(.width(10), .mode("unsigned")) comparator_9 (
    .a(10'h8), .b(counter_1_q), .lt(comparator_9_lt));  // open: gt, eq
  Comparator #(.width(10), .mode("unsigned")) comparator_10 (
    .a(10'h9), .b(counter_1_q), .lt(comparator_10_lt));  // open: gt, eq
  Comparator #(.width(10), .mode("unsigned")) comparator_11 (
    .a(10'h10), .b(counter_1_q), .lt(comparator_11_lt));  // open: gt, eq
  not not_1 (not_1_out, comparator_1_lt);
  not not_2 (not_2_out, comparator_2_lt);
  not not_3 (not_3_out, comparator_3_lt);
  not not_4 (not_4_out, comparator_4_lt);
  not not_5 (not_5_out, comparator_5_lt);
  not not_6 (not_6_out, comparator_6_lt);
  not not_7 (not_7_out, comparator_7_lt);
  not not_8 (not_8_out, comparator_8_lt);
  not not_9 (not_9_out, comparator_9_lt);
  not not_10 (not_10_out, comparator_10_lt);
  not not_11 (not_11_out, comparator_11_lt);
  Multiplexer #(.width(10), .enable("false")) multiplexer_1 (
    .in0({10{1'b0}}), .in1({10{1'b0}}), .sel(not_1_out));  // open: out
  Multiplexer #(.width(10), .enable("false")) multiplexer_2 (
    .in0({10{1'b0}}), .in1({10{1'b1}}), .out(h1), .sel(not_2_out));
  Multiplexer #(.width(10), .enable("false")) multiplexer_3 (
    .in0({10{1'b0}}), .in1(10'h201), .out(h2), .sel(not_3_out));
  Multiplexer #(.width(10), .enable("false")) multiplexer_4 (
    .in0({10{1'b0}}), .in1(10'h221), .out(h3), .sel(not_4_out));
  Multiplexer #(.width(10), .enable("false")) multiplexer_5 (
    .in0({10{1'b0}}), .in1(10'h2ac), .out(h4), .sel(not_5_out));
  Multiplexer #(.width(10), .enable("false")) multiplexer_6 (
    .in0({10{1'b0}}), .in1(10'h3f8), .out(h5), .sel(not_6_out));
  Multiplexer #(.width(10), .enable("false")) multiplexer_7 (
    .in0({10{1'b0}}), .in1(10'h2ac), .out(h6), .sel(not_7_out));
  Multiplexer #(.width(10), .enable("false")) multiplexer_8 (
    .in0({10{1'b0}}), .in1(10'h220), .out(h7), .sel(not_8_out));
  Multiplexer #(.width(10), .enable("false")) multiplexer_9 (
    .in0({10{1'b0}}), .in1(10'h200), .out(h8), .sel(not_9_out));
  Multiplexer #(.width(10), .enable("false")) multiplexer_10 (
    .in0({10{1'b0}}), .in1(10'h280), .out(h9), .sel(not_10_out));
  Multiplexer #(.width(10), .enable("false")) multiplexer_11 (
    .in0({10{1'b0}}), .in1(10'h380), .out(h10), .sel(not_11_out));
endmodule
