// Logisim project ScoreDisplay.circ as structural Verilog: 2 circuits, main circuit ScoreDisplay
module Synchroniser (
  input  bi,
  output bo
);

  wire and_2_out, and_3_out, clock_1_out, not_1_out, not_2_out, not_3_out, not_4_out, not_5_out;
  wire [1:0] and_4_out, register_1_q;

  not not_1 (not_1_out, register_1_q[1]);
  not not_2 (not_2_out, register_1_q[1]);
  not not_3 (not_3_out, register_1_q[0]);
  not not_4 (not_4_out, register_1_q[1]);
  not not_5 (not_5_out, register_1_q[0]);
  Register #(.width(2)) register_1 (.D(and_4_out), .Q(register_1_q), .clk(clock_1_out));  // open: en, clr
  Clock clock_1 (.out(clock_1_out));
  and and_1 (bo, not_1_out, register_1_q[0]);
  and and_2 (and_2_out, bi, not_2_out, register_1_q[0]);
  and and_3 (and_3_out, bi, not_3_out, register_1_q[1]);
  and and_4 (and_4_out[0], bi, not_4_out, not_5_out);
  or or_1 (and_4_out[1], and_2_out, and_3_out);

  // Notes on the sheet:
  //   --This is the Button Press Synchronizer from chapter 3 page 47--
  //   --Go back to the main file to play the game--
endmodule

module ScoreDisplay (
  input  Pulse,
  input  Reset_Score,
  output a,
  output b,
  output c,
  output d,
  output e,
  output f,
  output g
);

  wire and_1_out, and_2_out, and_3_out, and_4_out, and_5_out, and_6_out, and_7_out, and_8_out, and_9_out,
       and_10_out, and_11_out, and_12_out, and_13_out, and_14_out, and_15_out, and_16_out, and_17_out,
       and_18_out, and_19_out, and_20_out, and_21_out, and_22_out, and_23_out, and_24_out, and_25_out,
       and_26_out, not_1_out, not_2_out, not_3_out, not_4_out, not_5_out, not_6_out, not_7_out, not_8_out,
       not_9_out, not_10_out, not_11_out, not_12_out, not_13_out, not_14_out, not_15_out, not_16_out,
       not_17_out, not_18_out, not_19_out, not_20_out, not_21_out, not_22_out, not_23_out, not_24_out,
       not_25_out, not_26_out, not_27_out, not_28_out, not_29_out, not_30_out, not_31_out, not_32_out,
       not_33_out, not_34_out, not_35_out, not_36_out, not_37_out, not_38_out, not_39_out, not_40_out,
       not_41_out, not_42_out, not_43_out, not_44_out, not_45_out, not_46_out, not_47_out, not_48_out,
       not_49_out, not_50_out, not_51_out, not_52_out, synchroniser_1_bo, synchroniser_2_bo;
  wire [3:0] bit_extender_1_out, counter_1_q;

  Synchroniser synchroniser_1 (.bi(Pulse), .bo(synchroniser_1_bo));
  Synchroniser synchroniser_2 (.bi(Pulse), .bo(synchroniser_2_bo));
  assign bit_extender_1_out = {{3{1'b0}}, synchroniser_1_bo};  // Bit_Extender bit_extender_1
  Counter #(.width(4), .max('hf)) counter_1 (
    .D(bit_extender_1_out), .Q(counter_1_q), .clk(synchroniser_2_bo), .clr(Reset_Score));  // open: load, count, carry
  not not_1 (not_1_out, counter_1_q[3]);
  not not_2 (not_2_out, counter_1_q[2]);
  and and_1 (and_1_out, not_1_out, not_2_out, not_3_out);
  not not_3 (not_3_out, counter_1_q[0]);
  not not_4 (not_4_out, counter_1_q[3]);
  and and_2 (and_2_out, not_4_out, counter_1_q[1]);
  not not_5 (not_5_out, counter_1_q[3]);
  and and_3 (and_3_out, not_5_out, counter_1_q[2], counter_1_q[0]);
  and and_4 (and_4_out, counter_1_q[3], not_6_out, not_7_out);
  not not_6 (not_6_out, counter_1_q[2]);
  not not_7 (not_7_out, counter_1_q[1]);
  not not_8 (not_8_out, counter_1_q[3]);
  and and_5 (and_5_out, not_8_out, not_9_out);
  not not_9 (not_9_out, counter_1_q[2]);
  not not_10 (not_10_out, counter_1_q[3]);
  and and_6 (and_6_out, not_10_out, not_11_out, not_12_out);
  not not_11 (not_11_out, counter_1_q[1]);
  not not_12 (not_12_out, counter_1_q[0]);
  not not_13 (not_13_out, counter_1_q[2]);
  and and_7 (and_7_out, not_13_out, not_14_out);
  not not_14 (not_14_out, counter_1_q[1]);
  not not_15 (not_15_out, counter_1_q[3]);
  and and_8 (and_8_out, not_15_out, counter_1_q[1], counter_1_q[0]);
  not not_16 (not_16_out, counter_1_q[2]);
  and and_9 (and_9_out, not_16_out, not_17_out);
  not not_17 (not_17_out, counter_1_q[1]);
  not not_18 (not_18_out, counter_1_q[3]);
  and and_10 (and_10_out, not_18_out, counter_1_q[0]);
  not not_19 (not_19_out, counter_1_q[3]);
  and and_11 (and_11_out, not_19_out, counter_1_q[2]);
  not not_20 (not_20_out, counter_1_q[3]);
  not not_21 (not_21_out, counter_1_q[2]);
  not not_22 (not_22_out, counter_1_q[0]);
  not not_23 (not_23_out, counter_1_q[3]);
  not not_24 (not_24_out, counter_1_q[2]);
  not not_25 (not_25_out, counter_1_q[3]);
  not not_26 (not_26_out, counter_1_q[0]);
  not not_27 (not_27_out, counter_1_q[3]);
  not not_28 (not_28_out, counter_1_q[1]);
  not not_29 (not_29_out, counter_1_q[2]);
  not not_30 (not_30_out, counter_1_q[1]);
  not not_31 (not_31_out, counter_1_q[2]);
  not not_32 (not_32_out, counter_1_q[1]);
  and and_12 (and_12_out, not_31_out, not_32_out, not_33_out);
  not not_33 (not_33_out, counter_1_q[0]);
  not not_34 (not_34_out, counter_1_q[3]);
  and and_13 (and_13_out, not_34_out, counter_1_q[1], not_35_out);
  not not_35 (not_35_out, counter_1_q[0]);
  not not_36 (not_36_out, counter_1_q[3]);
  and and_14 (and_14_out, not_36_out, not_37_out, not_38_out);
  not not_37 (not_37_out, counter_1_q[1]);
  not not_38 (not_38_out, counter_1_q[0]);
  not not_39 (not_39_out, counter_1_q[3]);
  and and_15 (and_15_out, not_39_out, counter_1_q[2], not_40_out);
  not not_40 (not_40_out, counter_1_q[1]);
  not not_41 (not_41_out, counter_1_q[3]);
  and and_16 (and_16_out, not_41_out, counter_1_q[2], not_42_out);
  not not_42 (not_42_out, counter_1_q[0]);
  and and_17 (and_17_out, counter_1_q[3], not_43_out, not_44_out);
  not not_43 (not_43_out, counter_1_q[2]);
  not not_44 (not_44_out, counter_1_q[1]);
  not not_45 (not_45_out, counter_1_q[3]);
  not not_46 (not_46_out, counter_1_q[2]);
  and and_18 (and_18_out, not_45_out, not_46_out, counter_1_q[1]);
  not not_47 (not_47_out, counter_1_q[3]);
  and and_19 (and_19_out, not_47_out, counter_1_q[2], not_48_out);
  not not_48 (not_48_out, counter_1_q[1]);
  not not_49 (not_49_out, counter_1_q[3]);
  and and_20 (and_20_out, not_49_out, counter_1_q[2], not_50_out);
  not not_50 (not_50_out, counter_1_q[0]);
  not not_51 (not_51_out, counter_1_q[2]);
  and and_21 (and_21_out, counter_1_q[3], not_51_out, not_52_out);
  not not_52 (not_52_out, counter_1_q[1]);
  or or_1 (a, and_1_out, and_2_out, and_3_out, and_4_out);
  or or_2 (b, and_5_out, and_6_out, and_7_out, and_8_out);
  or or_3 (c, and_9_out, and_10_out, and_11_out);
  and and_22 (and_22_out, not_20_out, not_21_out, not_22_out);
  and and_23 (and_23_out, not_23_out, not_24_out, counter_1_q[1]);
  and and_24 (and_24_out, not_25_out, counter_1_q[1], not_26_out);
  and and_25 (and_25_out, not_27_out, counter_1_q[2], not_28_out, counter_1_q[0]);
  and and_26 (and_26_out, counter_1_q[3], not_29_out, not_30_out);
  or or_4 (e, and_12_out, and_13_out);
  or or_5 (f, and_14_out, and_15_out, and_16_out, and_17_out);
  or or_6 (g, and_18_out, and_19_out, and_20_out, and_21_out);
  or or_7 (d, and_22_out, and_23_out, and_24_out, and_25_out, and_26_out);
endmodule
