// Logisim project Synchroniser.circ as structural Verilog: 1 circuit, main circuit Synchroniser
module Synchroniser (
  input  bi,
  output bo
);

  wire and_2_out, and_3_out, clock_1_out, not_1_out, not_2_out, not_3_out, not_4_out, not_5_out;
  wire [1:0] and_4_out, register_1_q;

  not not_1 (not_1_out, register_1_q[1]);
  not not_2 (not_2_out, register_1_q[1]);
  not not_3 (not_3_out, register_1_q[0]);
  not not_4 (not_4_out, register_1_q[1]);
  not not_5 (not_5_out, register_1_q[0]);
  Register #(.width(2)) register_1 (.D(and_4_out), .Q(register_1_q), .clk(clock_1_out));  // open: en, clr
  Clock clock_1 (.out(clock_1_out));
  and and_1 (bo, not_1_out, register_1_q[0]);
  and and_2 (and_2_out, bi, not_2_out, register_1_q[0]);
  and and_3 (and_3_out, bi, not_3_out, register_1_q[1]);
  and and_4 (and_4_out[0], bi, not_4_out, not_5_out);
  or or_1 (and_4_out[1], and_2_out, and_3_out);

  // Notes on the sheet:
  //   --This is the Button Press Synchronizer from chapter 3 page 47--
  //   --Go back to the main file to play the game--
endmodule
