// Logisim project 1801042630.circ as structural Verilog: 1 circuit, main circuit Calculator
module Calculator (
  input  [15:0] A,
  input  [15:0] B,
  output [15:0] Result
);

  wire Clock_out, ControlUnit_la, ControlUnit_lb, ControlUnit_lmult, ControlUnit_sa, ControlUnit_smult,
       ControlUnit_sop, Datapath_gr, Datapath_leq, Reset_out, senkronizer_1_bo, Start_out;

  Button Reset (.out(Reset_out));
  Button Start (.out(Start_out));
  senkronizer senkronizer_1 (.bi(Start_out), .clock(Clock_out), .bo(senkronizer_1_bo));
  ControlUnit_main ControlUnit (
    .go(senkronizer_1_bo), .gr(Datapath_gr), .leq(Datapath_leq), .clk(Clock_out), .Sa(ControlUnit_sa),
    .Lb(ControlUnit_lb), .Smult(ControlUnit_smult), .Lmult(ControlUnit_lmult), .Sop(ControlUnit_sop),
    .La(ControlUnit_la));
  Clock Clock (.out(Clock_out));
  Datapath_main Datapath (
    .Smult(ControlUnit_smult), .Lmult(ControlUnit_lmult), .Sa(ControlUnit_sa), .in_5(A), .La(ControlUnit_la),
    .in_7(B), .Lb(ControlUnit_lb), .Sop(ControlUnit_sop), .clr(Reset_out), .clk(Clock_out), .gr(Datapath_gr),
    .leq(Datapath_leq), .Result(Result));

  // Notes on the sheet:
  //   Mehmet Avni ÇELİK
  //   1801042630
endmodule
