// Logisim project Datapath.circ as structural Verilog: 1 circuit, main circuit main
module main (
  input  clr,
  input  Smult,
  input  Lmult,
  input  Sa,
  input  [15:0] in_5,
  input  La,
  input  [15:0] in_7,
  input  Lb,
  input  clk,
  input  Sop,
  output gr,
  output leq,
  output [15:0] Result
);

  wire bitselector_1_out, bitselector_2_out, comparator_1_eq, comparator_1_lt, register_1_q, register_2_q,
       xnor_1_out;
  wire [15:0] adder_1_out, multiplexer_1_out, multiplexer_2_out, multiplexer_4_out, multiplexer_5_out,
       multiplexer_6_out, multiplexer_7_out, negator_1_out, negator_2_out, negator_3_out, register_3_q,
       register_4_q, register_5_q, register_6_q;

  Negator #(.width(16)) negator_1 (.in(register_6_q), .out(negator_1_out));
  Negator #(.width(16)) negator_2 (.in(in_5), .out(negator_2_out));
  Negator #(.width(16)) negator_3 (.in(in_7), .out(negator_3_out));
  Multiplexer #(.width(16), .enable("false")) multiplexer_1 (
    .in0(in_5), .in1(negator_2_out), .out(multiplexer_1_out), .sel(bitselector_1_out));
  BitSelector #(.width(16)) bitselector_1 (.in(in_5), .out(bitselector_1_out), .sel(4'b1111));
  Multiplexer #(.width(16), .enable("false")) multiplexer_2 (
    .in0(in_7), .in1(negator_3_out), .out(multiplexer_2_out), .sel(bitselector_2_out));
  BitSelector #(.width(16)) bitselector_2 (.in(in_7), .out(bitselector_2_out), .sel(4'b1111));
  Register #(.width(1)) register_1 (.D(bitselector_1_out), .Q(register_1_q), .clk(La));  // open: en, clr
  Register #(.width(1)) register_2 (.D(bitselector_2_out), .Q(register_2_q), .clk(Lb));  // open: en, clr
  Multiplexer #(.width(16), .enable("false")) multiplexer_3 (
    .in0(negator_1_out), .in1(register_6_q), .out(Result), .sel(xnor_1_out));
  xnor xnor_1 (xnor_1_out, register_1_q, register_2_q);
  Multiplexer #(.width(16), .enable("false")) multiplexer_4 (
    .in0({16{1'b0}}), .in1(adder_1_out), .out(multiplexer_4_out), .sel(Smult));
  Register #(.width(16)) register_3 (.D(multiplexer_5_out), .en(La), .Q(register_3_q), .clk(clk), .clr(clr));
  Multiplexer #(.width(16), .enable("false")) multiplexer_5 (
    .in0(adder_1_out), .in1(multiplexer_1_out), .out(multiplexer_5_out), .sel(Sa));
  Register #(.width(16)) register_4 (.D(multiplexer_4_out), .en(Lmult), .Q(register_4_q), .clk(clk), .clr(clr));
  Register #(.width(16)) register_5 (.D(multiplexer_2_out), .en(Lb), .Q(register_5_q), .clk(clk), .clr(clr));
  Comparator #(.width(16)) comparator_1 (
    .a(register_3_q), .b({16{1'b0}}), .gt(gr), .eq(comparator_1_eq), .lt(comparator_1_lt));
  or or_1 (leq, comparator_1_eq, comparator_1_lt);
  Register #(.width(16)) register_6 (.D(register_4_q), .en(1'b1), .Q(register_6_q), .clk(clk), .clr(clr));
  Multiplexer #(.width(16), .enable("false")) multiplexer_6 (
    .in0(register_3_q), .in1(register_4_q), .out(multiplexer_6_out), .sel(Sop));
  Multiplexer #(.width(16), .enable("false")) multiplexer_7 (
    .in0({16{1'b1}}), .in1(register_5_q), .out(multiplexer_7_out), .sel(Sop));
  Adder #(.width(16)) adder_1 (.a(multiplexer_6_out), .b(multiplexer_7_out), .out(adder_1_out));  // open: cin, cout

  // Notes on the sheet:
  //   Below part is for absolute value
endmodule
