// Logisim project 1801042630.circ as structural Verilog: 3 circuits, main circuit main
module main (
);

  wire button_1_out, clock_1_out, controlunit_1_greenl, controlunit_1_orangel, controlunit_1_redl,
       controlunit_1_resett, datapath_1__3sn, datapath_1__7sn, datapath_1__37sn;

  Button button_1 (.out(button_1_out));
  Datapath datapath_1 (
    .resetT(controlunit_1_resett), .clock(clock_1_out), ._3sn(datapath_1__3sn), ._7sn(datapath_1__7sn),
    ._37sn(datapath_1__37sn));
  Clock clock_1 (.out(clock_1_out));
  ControlUnit controlunit_1 (
    .req(button_1_out), .p3s(datapath_1__3sn), .p7s(datapath_1__7sn), .p37s(datapath_1__37sn),
    .clock(clock_1_out), .resetT(controlunit_1_resett), .redL(controlunit_1_redl),
    .orangeL(controlunit_1_orangel), .greenL(controlunit_1_greenl));
  LED led_1 (.in(controlunit_1_redl));
  LED led_2 (.in(controlunit_1_orangel));
  LED led_3 (.in(controlunit_1_greenl));
endmodule

module ControlUnit (
  input  req,
  input  p3s,
  input  p7s,
  input  p37s,
  input  clock,
  output resetT,
  output redL,
  output orangeL,
  output greenL
);

  wire and_1_out, and_2_out, and_3_out, and_4_out, and_5_out, and_6_out, and_7_out, not_1_out, not_2_out,
       not_3_out, not_4_out, not_5_out, not_6_out, not_7_out, S1_out;
  wire [1:0] N0_out, register_1_q;

  Register #(.width(2)) register_1 (.D(N0_out), .Q(register_1_q), .clk(clock));  // open: en, clr
  not not_1 (not_1_out, register_1_q[1]);
  not not_2 (not_2_out, register_1_q[0]);
  not not_3 (not_3_out, p37s);
  not not_4 (not_4_out, p3s);
  and and_1 (and_1_out, not_1_out, not_2_out, req);
  and and_2 (and_2_out, not_1_out, register_1_q[0], not_4_out);
  and and_3 (and_3_out, register_1_q[1], not_2_out, p7s);
  and and_4 (and_4_out, register_1_q[1], register_1_q[0], not_3_out);
  not not_5 (not_5_out, register_1_q[1]);
  not not_6 (not_6_out, register_1_q[0]);
  not not_7 (not_7_out, p37s);
  and and_5 (and_5_out, not_5_out, register_1_q[0], p3s);
  and and_6 (and_6_out, register_1_q[1], not_6_out);
  and and_7 (and_7_out, register_1_q[1], register_1_q[0], not_7_out);
  or N0 (N0_out[0], and_1_out, and_2_out, and_3_out, and_4_out);
  or N1 (N0_out[1], and_5_out, and_6_out, and_7_out);
  and S0 (resetT, not_1_out, not_2_out);
  and S1 (S1_out, not_1_out, register_1_q[0]);
  and S2 (orangeL, register_1_q[1], not_2_out);
  and S3 (greenL, register_1_q[1], register_1_q[0]);
  or N0_2 (redL, resetT, S1_out);
endmodule

module Datapath (
  input  resetT,
  input  clock,
  output _3sn,
  output _7sn,
  output _37sn
);

  wire undriven;
  wire [7:0] counter_1_q;

  Counter counter_1 (.D({8{1'b0}}), .count(undriven), .Q(counter_1_q), .clk(clock), .clr(resetT));  // open: load, carry
  Comparator comparator_1 (.a(counter_1_q), .b(8'h3), .eq(_3sn));  // open: gt, lt
  Comparator comparator_2 (.a(counter_1_q), .b(8'h7), .eq(_7sn));  // open: gt, lt
  Comparator comparator_3 (.a(counter_1_q), .b(8'h25), .eq(_37sn));  // open: gt, lt
endmodule
